// Logisim project cpu.circ as structural Verilog: 1 circuit, main circuit main
module main (
);

  wire and_1_out, and_2_out, and_4_out, and_6_out, and_7_out, and_10_out, and_11_out, and_12_out, and_13_out,
       and_14_out, and_20_out, bit_extender_7_out, CLK, comparator_1_eq, d_ff_1_q, d_ff_2_q, decoder_1_out1,
       decoder_1_out2, decoder_1_out3, decoder_1_out4, decoder_1_out5, decoder_1_out6, decoder_1_out7,
       decoder_1_out8, decoder_1_out9, decoder_1_out10, decoder_1_out11, decoder_1_out12, decoder_1_out13,
       decoder_1_out14, decoder_1_out15, decoder_1_out16, decoder_2_out1, decoder_2_out2, decoder_2_out3,
       decoder_2_out4, decoder_2_out5, decoder_2_out6, decoder_2_out7, decoder_2_out8, decoder_2_out9,
       decoder_2_out10, decoder_2_out11, decoder_2_out12, decoder_2_out13, decoder_2_out14, decoder_2_out15,
       decoder_2_out16, DRAW, DRAW_CLEAR, IR_W, is_alu, is_mul, KB_READ, LOAD_ROM, loading_rom, MEM_OVERRIDE,
       MEM_W, or_2_out, or_5_out, or_6_out, or_9_out, or_11_out, or_13_out, or_15_out, or_17_out, or_21_out,
       or_23_out, or_25_out, or_27_out, or_29_out, or_31_out, or_33_out, or_35_out, or_37_out, or_39_out,
       or_40_out, or_41_out, PC_INC, PC_W, PC_ZERO, rgb_video_1_p1, RST, RST_BTN, WR_R1, xor_1_out;
  wire [3:0] bit_extender_6_out;
  wire [4:0] alu_1_zero, and_24_out, and_25_out, bit_extender_15_out, bit_extender_16_out, OPC, R1, R2, RA1,
       RA2;
  wire [6:0] KEY;
  wire [7:0] DRAW_X, DRAW_Y;
  wire [15:0] imm;
  wire [23:0] bit_extender_1_out, bit_extender_2_out, DRAW_COLOR, RAM_ADDR;
  wire [31:0] adder_1_out, ALU_out, and_15_out, and_16_out, and_17_out, and_18_out, and_19_out, and_26_out,
       and_27_out, and_28_out, and_29_out, and_30_out, and_31_out, and_32_out, and_33_out, and_34_out,
       and_35_out, and_36_out, and_37_out, and_38_out, and_39_out, and_40_out, and_41_out, and_42_out,
       and_43_out, and_44_out, and_45_out, and_46_out, and_47_out, and_48_out, and_49_out, and_50_out,
       and_51_out, and_52_out, and_53_out, and_54_out, and_55_out, and_56_out, and_57_out,
       bit_extender_5_out, bit_extender_8_out, bit_extender_9_out, bit_extender_10_out, bit_extender_11_out,
       bit_extender_12_out, bit_extender_13_out, bit_extender_14_out, bit_extender_17_out,
       bit_extender_18_out, bit_extender_19_out, bit_extender_20_out, bit_extender_21_out,
       bit_extender_22_out, bit_extender_23_out, bit_extender_24_out, bit_extender_25_out,
       bit_extender_26_out, bit_extender_27_out, bit_extender_28_out, bit_extender_29_out,
       bit_extender_30_out, bit_extender_31_out, bit_extender_32_out, bit_extender_33_out,
       bit_extender_34_out, bit_extender_35_out, bit_extender_36_out, bit_extender_37_out,
       bit_extender_38_out, bit_extender_39_out, bit_extender_40_out, bit_extender_41_out,
       bit_extender_42_out, bit_extender_43_out, bit_extender_44_out, bit_extender_45_out,
       bit_extender_46_out, bit_extender_47_out, bit_extender_48_out, flags, JMP_DST, MEM_ADDR,
       multiplexer_1_out, multiplexer_2_out, multiplexer_3_out, multiplexer_8_out, or_10_out, or_12_out,
       or_14_out, or_16_out, or_18_out, or_19_out, or_20_out, or_22_out, or_24_out, or_26_out, or_28_out,
       or_30_out, or_32_out, or_34_out, or_36_out, or_38_out, PC, rA, RAM_D, rB, rC, rD, rE, REG_R2,
       register_3_q, rF, rG, rH, rI, rJ, rK, rL, rM, rN, rO, rom_1_data, rP, WD1, WD2;
  wire [31:16] REG_R1;
  wire [31:31] register_1_q;

  Clock clock_1 (.out(CLK));
  Button button_1 (.out(RST_BTN));
  Button button_2 (.out(LOAD_ROM));
  Keyboard keyboard_1 (.clk(CLK), .re(KB_READ), .clr(RST), .data(KEY));  // open: avail
  ROM #(.addrWidth(24), .dataWidth(32)) rom_1 (.addr(bit_extender_1_out), .data(rom_1_data));
  Bit_Extender #(.in_width(32), .out_width(24), .\type ("zero")) bit_extender_1 (.in(PC), .out(bit_extender_1_out));
  // RGB_Video #(.cursor("No Cursor"), .height(256), .width(256)) rgb_video_1: pin names not known; wires that end beside it: rgb_video_1_p1, CLK, DRAW, DRAW_X, DRAW_Y, DRAW_COLOR
  or or_1 (rgb_video_1_p1, DRAW_CLEAR, RST);
  Bit_Extender #(.in_width(32), .out_width(24), .\type ("zero")) bit_extender_2 (.in(PC), .out(bit_extender_2_out));
  D_Flip_Flop d_ff_1 (.D(LOAD_ROM), .clk(or_2_out), .Q(d_ff_1_q));  // open: Qn, preset, reset
  or or_2 (or_2_out, LOAD_ROM, CLK);
  Comparator #(.width(24)) comparator_1 (.a(24'h19), .b(bit_extender_2_out), .eq(comparator_1_eq));  // open: gt, lt
  and and_1 (and_1_out, ~comparator_1_eq, loading_rom);  // AND_Gate
  or or_3 (loading_rom, d_ff_1_q, and_1_out);
  or or_4 (RST, RST_BTN, and_2_out);
  and and_2 (and_2_out, loading_rom, comparator_1_eq);
  // Probe on PC
  // Probe on PC_INC
  // Probe on RAM_ADDR
  // Probe on IR_W
  // Probe on RAM_D
  Register #(.width(32)) register_1 (
    .D(RAM_D), .en(IR_W), .clk(CLK), .Q({register_1_q[31], OPC, R1, R2, imm}), .clr(RST));
  // Probe on R1
  // Probe on R2
  // Probe on imm[15:11]
  // Probe on imm[10:6]
  // Probe on imm
  or or_5 (or_5_out, loading_rom, MEM_W);
  Bit_Extender #(.in_width(32), .out_width(24)) bit_extender_3 (.in(REG_R2), .out(DRAW_COLOR));
  Multiplexer #(.width(32)) multiplexer_1 (.in0(PC), .in1(MEM_ADDR), .out(multiplexer_1_out), .sel(MEM_OVERRIDE));
  not not_1 (is_alu, register_1_q[31]);
  // Probe on {REG_R1, DRAW_X, DRAW_Y}
  // Probe on REG_R2
  // Probe on flags
  Bit_Extender #(.in_width(32), .out_width(24), .\type ("zero")) bit_extender_4 (
    .in(multiplexer_1_out), .out(RAM_ADDR));
  Multiplexer #(.width(32)) multiplexer_2 (.in0(rom_1_data), .in1(REG_R2), .out(multiplexer_2_out), .sel(MEM_OVERRIDE));
  RAM #(.addrWidth(24), .asyncread("true"), .dataWidth(32)) ram_1 (
    .addr(RAM_ADDR), .we(or_5_out), .oe(1'b1), .clk(CLK), .din(multiplexer_2_out), .dout(RAM_D));
  // Probe on rA
  // Probe on rB
  // Probe on rC
  // Probe on rD
  // Probe on rE
  // Probe on rF
  // Probe on rG
  // Probe on rH
  // Probe on rI
  // Probe on rJ
  // Probe on rK
  // Probe on rL
  // Probe on rM
  // Probe on rN
  // Probe on rO
  // Probe on rP
  Multiplexer #(.width(32)) multiplexer_3 (
    .in0(REG_R2), .in1(bit_extender_5_out), .out(multiplexer_3_out), .sel(OPC[4]));
  assign bit_extender_5_out = {{16{1'b0}}, imm};  // Bit_Extender bit_extender_5
  Bit_Extender #(.in_width(5), .out_width(4)) bit_extender_6 (.in(OPC), .out(bit_extender_6_out));
  and and_3 (is_mul, OPC[2], OPC[3], is_alu);
  and and_4 (and_4_out, OPC[4], ~OPC[3]);  // AND_Gate
  and and_5 (KB_READ, OPC[4], OPC[3], OPC[2], ~OPC[1]);  // AND_Gate
  and and_6 (and_6_out, ~OPC[4], ~OPC[3], ~OPC[2], ~OPC[1], ~OPC[0]);  // AND_Gate
  and and_7 (and_7_out, ~OPC[4], ~OPC[3], OPC[2], OPC[1], OPC[0], MEM_OVERRIDE);  // AND_Gate
  and and_8 (DRAW, ~is_alu, OPC[4], OPC[3], OPC[2], OPC[1], ~OPC[0]);  // AND_Gate
  and and_9 (DRAW_CLEAR, ~is_alu, OPC[4], OPC[3], OPC[2], OPC[1], OPC[0]);  // AND_Gate
  and and_10 (and_10_out, KB_READ, ~is_alu);  // AND_Gate
  and and_11 (and_11_out, and_6_out, ~is_alu);  // AND_Gate
  xor xor_1 (xor_1_out, OPC[0], bit_extender_7_out);
  Bit_Extender #(.in_width(32), .out_width(1)) bit_extender_7 (.in(flags), .out(bit_extender_7_out));
  and and_12 (and_12_out, ~is_alu, ~OPC[4], ~OPC[3], OPC[2]);  // AND_Gate
  assign bit_extender_8_out = {{31{is_alu}}, is_alu};  // Bit_Extender bit_extender_8
  assign bit_extender_9_out = {{25{1'b0}}, KEY};  // Bit_Extender bit_extender_9
  assign bit_extender_10_out = {{31{and_10_out}}, and_10_out};  // Bit_Extender bit_extender_10
  assign bit_extender_11_out = {{31{and_11_out}}, and_11_out};  // Bit_Extender bit_extender_11
  assign bit_extender_12_out = {{31{and_13_out}}, and_13_out};  // Bit_Extender bit_extender_12
  and and_13 (and_13_out, and_4_out, ~is_alu);  // AND_Gate
  and and_14 (and_14_out, ~is_alu, OPC[3], ~OPC[2], or_6_out);  // AND_Gate
  not not_2 (PC_INC, and_14_out);
  or or_6 (or_6_out, ~OPC[1], xor_1_out);  // OR_Gate
  Multiplexer #(.width(32)) multiplexer_4 (
    .in0({REG_R1, DRAW_X, DRAW_Y}), .in1(bit_extender_13_out), .out(JMP_DST), .sel(OPC[4]));
  assign bit_extender_13_out = {{16{1'b0}}, imm};  // Bit_Extender bit_extender_13
  D_Flip_Flop d_ff_2 (.D(PC_W), .clk(CLK), .Q(d_ff_2_q), .reset(RST));  // open: Qn, preset
  alu alu_1 (
    .Sel(bit_extender_6_out), .A({REG_R1, DRAW_X, DRAW_Y}), .B(multiplexer_3_out), .Cin(1'b0),
    .Cout(alu_1_zero[3]), .Aout(ALU_out), .Zero(alu_1_zero[0]), .sign(alu_1_zero[4]), .Hout(WD2));
  or or_7 (WR_R1, is_alu, and_4_out, KB_READ, and_6_out, and_7_out);
  assign and_15_out = ALU_out & bit_extender_8_out;  // AND_Gate and_15, 32 bits wide
  assign and_16_out = bit_extender_9_out & bit_extender_10_out;  // AND_Gate and_16, 32 bits wide
  assign and_17_out = REG_R2 & bit_extender_11_out;  // AND_Gate and_17, 32 bits wide
  assign and_18_out = {imm, {16{1'b0}}} & bit_extender_12_out;  // AND_Gate and_18, 32 bits wide
  assign and_19_out = bit_extender_14_out & RAM_D;  // AND_Gate and_19, 32 bits wide
  assign bit_extender_14_out = {{31{and_20_out}}, and_20_out};  // Bit_Extender bit_extender_14
  and and_20 (and_20_out, MEM_OVERRIDE, ~MEM_W);  // AND_Gate
  and and_21 (MEM_OVERRIDE, and_12_out, d_ff_2_q);
  Multiplexer #(.select(2), .width(5)) multiplexer_5 (
    .in0(R1), .in1(R2), .in3(imm[15:11]), .out(RA1), .sel({is_mul, is_alu}));  // open: in2
  Multiplexer #(.select(2), .width(5)) multiplexer_6 (
    .in0(R2), .in1(imm[15:11]), .in3(imm[10:6]), .out(RA2), .sel({is_mul, is_alu}));  // open: in2
  assign WD1 = and_15_out | and_16_out | and_17_out | and_18_out | and_19_out | {32{1'b0}};  // OR_Gate or_8, 32 bits wide
  Multiplexer #(.width(32)) multiplexer_7 (.in0({REG_R1, DRAW_X, DRAW_Y}), .in1(REG_R2), .out(MEM_ADDR), .sel(OPC[1]));
  Adder #(.width(32)) adder_1 (.a(PC), .b(32'h1), .out(adder_1_out));  // open: cin, cout
  not not_3 (PC_W, MEM_OVERRIDE);
  Multiplexer #(.width(32)) multiplexer_8 (.in0(JMP_DST), .in1(adder_1_out), .out(multiplexer_8_out), .sel(PC_INC));
  and and_22 (IR_W, PC_W, ~loading_rom);  // AND_Gate
  and and_23 (MEM_W, MEM_OVERRIDE, ~OPC[1]);  // AND_Gate
  Register #(.width(32)) u_PC (.D(multiplexer_8_out), .en(PC_W), .clk(CLK), .Q(PC), .clr(RST));
  or or_9 (or_9_out, PC[0], PC[1], PC[2], PC[3], PC[4], PC[5], PC[6], PC[7], PC[8], PC[9], PC[10], PC[11], PC[12], PC[13], PC[14], PC[15], PC[16], PC[17], PC[18], PC[19], PC[20], PC[21], PC[22], PC[23], PC[24], PC[25], PC[26], PC[27], PC[28], PC[29], PC[30], PC[31]);
  not not_4 (PC_ZERO, or_9_out);
  assign bit_extender_15_out = {{4{WR_R1}}, WR_R1};  // Bit_Extender bit_extender_15
  assign bit_extender_16_out = {{4{is_mul}}, is_mul};  // Bit_Extender bit_extender_16
  Decoder #(.select(5)) decoder_1 (
    .out1(decoder_1_out1), .out2(decoder_1_out2), .out3(decoder_1_out3), .out4(decoder_1_out4),
    .out5(decoder_1_out5), .out6(decoder_1_out6), .out7(decoder_1_out7), .out8(decoder_1_out8),
    .out9(decoder_1_out9), .out10(decoder_1_out10), .out11(decoder_1_out11), .out12(decoder_1_out12),
    .out13(decoder_1_out13), .out14(decoder_1_out14), .out15(decoder_1_out15), .out16(decoder_1_out16),
    .sel(and_24_out));  // open: out0, out17, out18, out19, out20, out21, out22, out23, out24, out25, out26, out27, out28, out29, out30, out31, en
  assign and_24_out = R1 & bit_extender_15_out;  // AND_Gate and_24, 5 bits wide
  Decoder #(.select(5)) decoder_2 (
    .out1(decoder_2_out1), .out2(decoder_2_out2), .out3(decoder_2_out3), .out4(decoder_2_out4),
    .out5(decoder_2_out5), .out6(decoder_2_out6), .out7(decoder_2_out7), .out8(decoder_2_out8),
    .out9(decoder_2_out9), .out10(decoder_2_out10), .out11(decoder_2_out11), .out12(decoder_2_out12),
    .out13(decoder_2_out13), .out14(decoder_2_out14), .out15(decoder_2_out15), .out16(decoder_2_out16),
    .sel(and_25_out));  // open: out0, out17, out18, out19, out20, out21, out22, out23, out24, out25, out26, out27, out28, out29, out30, out31, en
  assign and_25_out = R2 & bit_extender_16_out;  // AND_Gate and_25, 5 bits wide
  assign and_26_out = WD1 & bit_extender_17_out;  // AND_Gate and_26, 32 bits wide
  assign bit_extender_17_out = {{31{decoder_1_out1}}, decoder_1_out1};  // Bit_Extender bit_extender_17
  assign and_27_out = WD2 & bit_extender_18_out;  // AND_Gate and_27, 32 bits wide
  assign bit_extender_18_out = {{31{decoder_2_out1}}, decoder_2_out1};  // Bit_Extender bit_extender_18
  assign and_28_out = WD1 & bit_extender_19_out;  // AND_Gate and_28, 32 bits wide
  assign bit_extender_19_out = {{31{decoder_1_out2}}, decoder_1_out2};  // Bit_Extender bit_extender_19
  assign and_29_out = WD2 & bit_extender_20_out;  // AND_Gate and_29, 32 bits wide
  assign bit_extender_20_out = {{31{decoder_2_out2}}, decoder_2_out2};  // Bit_Extender bit_extender_20
  assign and_30_out = WD1 & bit_extender_21_out;  // AND_Gate and_30, 32 bits wide
  assign bit_extender_21_out = {{31{decoder_1_out3}}, decoder_1_out3};  // Bit_Extender bit_extender_21
  assign and_31_out = WD2 & bit_extender_22_out;  // AND_Gate and_31, 32 bits wide
  assign bit_extender_22_out = {{31{decoder_2_out3}}, decoder_2_out3};  // Bit_Extender bit_extender_22
  assign and_32_out = WD1 & bit_extender_23_out;  // AND_Gate and_32, 32 bits wide
  assign bit_extender_23_out = {{31{decoder_1_out4}}, decoder_1_out4};  // Bit_Extender bit_extender_23
  assign and_33_out = WD2 & bit_extender_24_out;  // AND_Gate and_33, 32 bits wide
  assign bit_extender_24_out = {{31{decoder_2_out4}}, decoder_2_out4};  // Bit_Extender bit_extender_24
  assign and_34_out = WD1 & bit_extender_25_out;  // AND_Gate and_34, 32 bits wide
  assign bit_extender_25_out = {{31{decoder_1_out5}}, decoder_1_out5};  // Bit_Extender bit_extender_25
  assign and_35_out = WD2 & bit_extender_26_out;  // AND_Gate and_35, 32 bits wide
  assign bit_extender_26_out = {{31{decoder_2_out5}}, decoder_2_out5};  // Bit_Extender bit_extender_26
  assign bit_extender_27_out = {{31{decoder_1_out6}}, decoder_1_out6};  // Bit_Extender bit_extender_27
  assign bit_extender_28_out = {{31{decoder_2_out6}}, decoder_2_out6};  // Bit_Extender bit_extender_28
  assign and_36_out = WD1 & bit_extender_29_out;  // AND_Gate and_36, 32 bits wide
  assign bit_extender_29_out = {{31{decoder_1_out7}}, decoder_1_out7};  // Bit_Extender bit_extender_29
  assign and_37_out = WD2 & bit_extender_30_out;  // AND_Gate and_37, 32 bits wide
  assign bit_extender_30_out = {{31{decoder_2_out7}}, decoder_2_out7};  // Bit_Extender bit_extender_30
  assign and_38_out = WD1 & bit_extender_31_out;  // AND_Gate and_38, 32 bits wide
  assign bit_extender_31_out = {{31{decoder_1_out8}}, decoder_1_out8};  // Bit_Extender bit_extender_31
  assign and_39_out = WD2 & bit_extender_32_out;  // AND_Gate and_39, 32 bits wide
  assign bit_extender_32_out = {{31{decoder_2_out8}}, decoder_2_out8};  // Bit_Extender bit_extender_32
  assign and_40_out = WD1 & bit_extender_33_out;  // AND_Gate and_40, 32 bits wide
  assign bit_extender_33_out = {{31{decoder_1_out9}}, decoder_1_out9};  // Bit_Extender bit_extender_33
  assign and_41_out = WD2 & bit_extender_34_out;  // AND_Gate and_41, 32 bits wide
  assign bit_extender_34_out = {{31{decoder_2_out9}}, decoder_2_out9};  // Bit_Extender bit_extender_34
  assign and_42_out = WD1 & bit_extender_35_out;  // AND_Gate and_42, 32 bits wide
  assign bit_extender_35_out = {{31{decoder_1_out10}}, decoder_1_out10};  // Bit_Extender bit_extender_35
  assign and_43_out = WD2 & bit_extender_36_out;  // AND_Gate and_43, 32 bits wide
  assign bit_extender_36_out = {{31{decoder_2_out10}}, decoder_2_out10};  // Bit_Extender bit_extender_36
  assign and_44_out = WD1 & bit_extender_37_out;  // AND_Gate and_44, 32 bits wide
  assign bit_extender_37_out = {{31{decoder_1_out11}}, decoder_1_out11};  // Bit_Extender bit_extender_37
  assign and_45_out = WD2 & bit_extender_38_out;  // AND_Gate and_45, 32 bits wide
  assign bit_extender_38_out = {{31{decoder_2_out11}}, decoder_2_out11};  // Bit_Extender bit_extender_38
  assign and_46_out = WD1 & bit_extender_39_out;  // AND_Gate and_46, 32 bits wide
  assign bit_extender_39_out = {{31{decoder_1_out12}}, decoder_1_out12};  // Bit_Extender bit_extender_39
  assign and_47_out = WD2 & bit_extender_40_out;  // AND_Gate and_47, 32 bits wide
  assign bit_extender_40_out = {{31{decoder_2_out12}}, decoder_2_out12};  // Bit_Extender bit_extender_40
  assign and_48_out = WD1 & bit_extender_41_out;  // AND_Gate and_48, 32 bits wide
  assign bit_extender_41_out = {{31{decoder_1_out13}}, decoder_1_out13};  // Bit_Extender bit_extender_41
  assign and_49_out = WD2 & bit_extender_42_out;  // AND_Gate and_49, 32 bits wide
  assign bit_extender_42_out = {{31{decoder_2_out13}}, decoder_2_out13};  // Bit_Extender bit_extender_42
  assign and_50_out = WD1 & bit_extender_43_out;  // AND_Gate and_50, 32 bits wide
  assign bit_extender_43_out = {{31{decoder_1_out14}}, decoder_1_out14};  // Bit_Extender bit_extender_43
  assign and_51_out = WD2 & bit_extender_44_out;  // AND_Gate and_51, 32 bits wide
  assign bit_extender_44_out = {{31{decoder_2_out14}}, decoder_2_out14};  // Bit_Extender bit_extender_44
  assign and_52_out = WD1 & bit_extender_45_out;  // AND_Gate and_52, 32 bits wide
  assign bit_extender_45_out = {{31{decoder_1_out15}}, decoder_1_out15};  // Bit_Extender bit_extender_45
  assign and_53_out = WD2 & bit_extender_46_out;  // AND_Gate and_53, 32 bits wide
  assign bit_extender_46_out = {{31{decoder_2_out15}}, decoder_2_out15};  // Bit_Extender bit_extender_46
  assign and_54_out = WD1 & bit_extender_47_out;  // AND_Gate and_54, 32 bits wide
  assign bit_extender_47_out = {{31{decoder_1_out16}}, decoder_1_out16};  // Bit_Extender bit_extender_47
  assign and_55_out = WD2 & bit_extender_48_out;  // AND_Gate and_55, 32 bits wide
  assign bit_extender_48_out = {{31{decoder_2_out16}}, decoder_2_out16};  // Bit_Extender bit_extender_48
  Register #(.width(32)) register_2 (
    .D({{27{1'b0}}, alu_1_zero[4:3], 2'b00, alu_1_zero[0]}), .en(is_alu), .clk(CLK), .Q(flags), .clr(RST));
  Register #(.width(32)) register_3 (.en(1'b0), .clk(CLK), .Q(register_3_q), .clr(RST));  // open: D
  Register #(.width(32)) register_4 (.D(or_10_out), .en(or_11_out), .clk(CLK), .Q(rA), .clr(RST));
  assign or_10_out = and_26_out | and_27_out;  // OR_Gate or_10, 32 bits wide
  or or_11 (or_11_out, decoder_1_out1, decoder_2_out1);
  Register #(.width(32)) register_5 (.D(or_12_out), .en(or_13_out), .clk(CLK), .Q(rB), .clr(RST));
  assign or_12_out = and_28_out | and_29_out;  // OR_Gate or_12, 32 bits wide
  or or_13 (or_13_out, decoder_1_out2, decoder_2_out2);
  Register #(.width(32)) register_6 (.D(or_14_out), .en(or_15_out), .clk(CLK), .Q(rC), .clr(RST));
  assign or_14_out = and_30_out | and_31_out;  // OR_Gate or_14, 32 bits wide
  or or_15 (or_15_out, decoder_1_out3, decoder_2_out3);
  Register #(.width(32)) register_7 (.D(or_16_out), .en(or_17_out), .clk(CLK), .Q(rD), .clr(RST));
  assign or_16_out = and_32_out | and_33_out;  // OR_Gate or_16, 32 bits wide
  or or_17 (or_17_out, decoder_1_out4, decoder_2_out4);
  assign or_18_out = and_34_out | and_35_out;  // OR_Gate or_18, 32 bits wide
  assign and_56_out = WD1 & bit_extender_27_out;  // AND_Gate and_56, 32 bits wide
  assign or_19_out = and_56_out | and_57_out;  // OR_Gate or_19, 32 bits wide
  assign and_57_out = WD2 & bit_extender_28_out;  // AND_Gate and_57, 32 bits wide
  Register #(.width(32)) register_8 (.D(or_20_out), .en(or_21_out), .clk(CLK), .Q(rG), .clr(RST));
  assign or_20_out = and_36_out | and_37_out;  // OR_Gate or_20, 32 bits wide
  or or_21 (or_21_out, decoder_1_out7, decoder_2_out7);
  Register #(.width(32)) register_9 (.D(or_22_out), .en(or_23_out), .clk(CLK), .Q(rH), .clr(RST));
  assign or_22_out = and_38_out | and_39_out;  // OR_Gate or_22, 32 bits wide
  or or_23 (or_23_out, decoder_1_out8, decoder_2_out8);
  Register #(.width(32)) register_10 (.D(or_24_out), .en(or_25_out), .clk(CLK), .Q(rI), .clr(RST));
  assign or_24_out = and_40_out | and_41_out;  // OR_Gate or_24, 32 bits wide
  or or_25 (or_25_out, decoder_1_out9, decoder_2_out9);
  Register #(.width(32)) register_11 (.D(or_26_out), .en(or_27_out), .clk(CLK), .Q(rJ), .clr(RST));
  assign or_26_out = and_42_out | and_43_out;  // OR_Gate or_26, 32 bits wide
  or or_27 (or_27_out, decoder_1_out10, decoder_2_out10);
  Register #(.width(32)) register_12 (.D(or_28_out), .en(or_29_out), .clk(CLK), .Q(rK), .clr(RST));
  assign or_28_out = and_44_out | and_45_out;  // OR_Gate or_28, 32 bits wide
  or or_29 (or_29_out, decoder_1_out11, decoder_2_out11);
  Register #(.width(32)) register_13 (.D(or_30_out), .en(or_31_out), .clk(CLK), .Q(rL), .clr(RST));
  assign or_30_out = and_46_out | and_47_out;  // OR_Gate or_30, 32 bits wide
  or or_31 (or_31_out, decoder_1_out12, decoder_2_out12);
  Register #(.width(32)) register_14 (.D(or_32_out), .en(or_33_out), .clk(CLK), .Q(rM), .clr(RST));
  assign or_32_out = and_48_out | and_49_out;  // OR_Gate or_32, 32 bits wide
  or or_33 (or_33_out, decoder_1_out13, decoder_2_out13);
  Register #(.width(32)) register_15 (.D(or_34_out), .en(or_35_out), .clk(CLK), .Q(rN), .clr(RST));
  assign or_34_out = and_50_out | and_51_out;  // OR_Gate or_34, 32 bits wide
  or or_35 (or_35_out, decoder_1_out14, decoder_2_out14);
  Register #(.width(32)) register_16 (.D(or_36_out), .en(or_37_out), .clk(CLK), .Q(rO), .clr(RST));
  assign or_36_out = and_52_out | and_53_out;  // OR_Gate or_36, 32 bits wide
  or or_37 (or_37_out, decoder_1_out15, decoder_2_out15);
  Register #(.width(32)) register_17 (.D(or_38_out), .en(or_39_out), .clk(CLK), .Q(rP), .clr(RST));
  assign or_38_out = and_54_out | and_55_out;  // OR_Gate or_38, 32 bits wide
  or or_39 (or_39_out, decoder_1_out16, decoder_2_out16);
  Register #(.width(32)) register_18 (.D(or_18_out), .en(or_40_out), .clk(CLK), .Q(rE), .clr(RST));
  or or_40 (or_40_out, decoder_1_out5, decoder_2_out5);
  Register #(.width(32)) register_19 (.D(or_19_out), .en(or_41_out), .clk(CLK), .Q(rF), .clr(RST));
  or or_41 (or_41_out, decoder_1_out6, decoder_2_out6);
  Multiplexer #(.select(5), .width(32)) multiplexer_9 (
    .in0(register_3_q), .in1(rA), .in2(rB), .in3(rC), .in4(rD), .in5(rE), .in6(rF), .in7(rG), .in8(rH),
    .in9(rI), .in10(rJ), .in11(rK), .in12(rL), .in13(rM), .in14(rN), .in15(rO), .in16(rP), .in30(PC),
    .in31(flags), .out({REG_R1, DRAW_X, DRAW_Y}), .sel(RA1));  // open: in17, in18, in19, in20, in21, in22, in23, in24, in25, in26, in27, in28, in29
  Multiplexer #(.select(5), .width(32)) multiplexer_10 (
    .in0(register_3_q), .in1(rA), .in2(rB), .in3(rC), .in4(rD), .in5(rE), .in6(rF), .in7(rG), .in8(rH),
    .in9(rI), .in10(rJ), .in11(rK), .in12(rL), .in13(rM), .in14(rN), .in15(rO), .in16(rP), .in30(PC),
    .in31(flags), .out(REG_R2), .sel(RA2));  // open: in17, in18, in19, in20, in21, in22, in23, in24, in25, in26, in27, in28, in29
  Demultiplexer demultiplexer_1 ();  // open: out0, out1, in, sel

  // Other names for the same wires on the sheet: R4[4:0] = imm[10:6]; R3[4:0] = imm[15:11];
  //   REG_R1[15:0] = {DRAW_X, DRAW_Y}

  // Notes on the sheet:
  //   contents of rom_1 (hex, n*v repeats v):
  //   48200015 c04000ff 4842ffff 48800000 48c0001f 48e00800 e0000011 0 4c080001 4cbf0001 30601140 f8830000
  //   15080000 2cc60000 28840000 ec000008 0 9d010000 28210000 e0000008 0 a5f0a5f0 e5f0a5f0 85f0a5f0
  //   8ff0a5f0
  //   keyboard input
  //   TV OUTPUT
  //   To start:
  //   Press RST
  //   Press LOAD_ROM
  //   Keep cycling to load
  //   Run cycles to run your program
  //   Load ROM from file and set ROM_TO_LOAD (right of ROM) to length
  //   Program will run automatically after RAM is loaded (keep cycling)
  //   REGISTERS
  //   MOVH
  //   READ
  //   MOV
  //   LW
  //   where do we jmp?
  //   do we jmp?
  //   LW AND SW support
  //   FLAGS
  //   ZERO
  //   A
  //   B
  //   C
  //   D
  //   G
  //   H
  //   I
  //   J
  //   K
  //   E
  //   F
  //   L
  //   M
  //   N
  //   O
  //   P
  //   shame koutek
endmodule
