// Logisim project test.circ as structural Verilog: 36 circuits, main circuit alu_test
module alu_test (
  input  [3:0] in_1,
  input  in_2
);

  wire alu_1_cout, alu_1_sign, alu_1_zero;
  wire [3:0] alu_1_aout, alu_1_aout_2, alu_1_aout_3, alu_1_aout_4;
  wire [31:0] register_1_q, register_2_q;
  wire [31:16] alu_1_aout_5;

  Register #(.width(32)) register_1 (.Q(register_1_q));  // open: D, en, clk, clr
  Register #(.width(32)) register_2 (.Q(register_2_q));  // open: D, en, clk, clr
  Hex_Digit_Display hex_digit_display_1 (.value(alu_1_aout_4));  // open: dp
  // Probe on alu_1_cout
  alu alu_1 (
    .Sel(in_1), .A(register_1_q), .B(register_2_q), .Cin(in_2), .Cout(alu_1_cout),
    .Aout({alu_1_aout_5, alu_1_aout_4, alu_1_aout_3, alu_1_aout_2, alu_1_aout}), .Zero(alu_1_zero),
    .sign(alu_1_sign));  // open: Hout
  Hex_Digit_Display hex_digit_display_2 (.value(alu_1_aout_3));  // open: dp
  Hex_Digit_Display hex_digit_display_3 (.value(alu_1_aout_2));  // open: dp
  // Probe on alu_1_zero
  // Probe on alu_1_sign
  Hex_Digit_Display hex_digit_display_4 (.value(alu_1_aout));  // open: dp
  // Probe on {alu_1_aout_5, alu_1_aout_4, alu_1_aout_3, alu_1_aout_2, alu_1_aout}
  // Pins of 16 and 32 bits meet at {alu_1_aout_5, alu_1_aout_4, alu_1_aout_3, alu_1_aout_2, alu_1_aout}
endmodule

module alu (
  input  [3:0] Sel,
  input  [31:0] A,
  input  [31:0] B,
  input  Cin,
  output Cout,
  output [31:0] Aout,
  output Zero,
  output sign,
  output [31:0] Hout
);

  wire addsub32_1_cout, is_mul_out, or_3_out, shl32_1_cout, shr32_1_cout;
  wire [31:0] addsub32_1_s, and_1_out, and_2_out, and_3_out, bit_extender_1_out, bit_extender_2_out,
       mul32_1_hout, mul32_1_lout, not_1_out, or_1_out, or_2_out, shl32_1_aout, shr32_1_aout, xor_1_out;

  assign bit_extender_1_out = {{31{Sel[1]}}, Sel[1]};  // Bit_Extender bit_extender_1
  assign and_1_out = 32'h1 & bit_extender_1_out;  // AND_Gate and_1, 32 bits wide
  assign and_2_out = B & ~bit_extender_1_out;  // AND_Gate and_2, 32 bits wide
  assign or_1_out = and_1_out | and_2_out;  // OR_Gate or_1, 32 bits wide
  assign not_1_out = ~A;  // NOT_Gate not_1, 32 bits wide
  assign xor_1_out = A ^ B;  // XOR_Gate xor_1, 32 bits wide
  assign or_2_out = A | B;  // OR_Gate or_2, 32 bits wide
  assign and_3_out = A & B;  // AND_Gate and_3, 32 bits wide
  mux4x32 mux4x32_1 (
    .sel(Sel), .in_2(not_1_out), .in_3(xor_1_out), .in_4(or_2_out), .in_5(and_3_out), .in_6(shl32_1_aout),
    .in_7(shr32_1_aout), .in_8(shl32_1_aout), .in_9(shr32_1_aout), .in_10(addsub32_1_s),
    .in_11(addsub32_1_s), .in_12(addsub32_1_s), .in_13(addsub32_1_s), .in_14(mul32_1_lout), .out_18(Aout));  // open: in_15, in_16, in_17
  addsub32 addsub32_1 (.A(A), .B(or_1_out), .Cin(Cin), .sub(Sel[0]), .S(addsub32_1_s), .Cout(addsub32_1_cout));
  shl32 shl32_1 (.A(A), .Cin(Cin), .isRot(Sel[1]), .Aout(shl32_1_aout), .Cout(shl32_1_cout));
  shr32 shr32_1 (.A(A), .Cin(Cin), .isRot(Sel[1]), .Aout(shr32_1_aout), .Cout(shr32_1_cout));
  mul32 mul32_1 (.A(A), .B(B), .Lout(mul32_1_lout), .Hout(mul32_1_hout));
  mux4x1 mux4x1_1 (
    .sel(Sel), .in_2(1'b0), .in_3(1'b0), .in_4(1'b0), .in_5(1'b0), .in_6(shl32_1_cout), .in_7(shr32_1_cout),
    .in_8(shl32_1_cout), .in_9(shr32_1_cout), .in_10(addsub32_1_cout), .in_11(addsub32_1_cout),
    .in_12(addsub32_1_cout), .in_13(addsub32_1_cout), .in_14(1'b0), .in_15(1'b0), .in_16(1'b0), .in_17(1'b0),
    .out_18(Cout));
  and is_mul (is_mul_out, ~Sel[0], ~Sel[1], Sel[2], Sel[3]);  // AND_Gate
  assign bit_extender_2_out = {{31{is_mul_out}}, is_mul_out};  // Bit_Extender bit_extender_2
  assign Hout = bit_extender_2_out & mul32_1_hout;  // AND_Gate and_4, 32 bits wide
  or or_3 (or_3_out, Aout[0], Aout[1], Aout[2], Aout[3], Aout[4], Aout[5], Aout[6], Aout[7], Aout[8], Aout[9], Aout[10], Aout[11], Aout[12], Aout[13], Aout[14], Aout[15], Aout[16], Aout[17], Aout[18], Aout[19], Aout[20], Aout[21], Aout[22], Aout[23], Aout[24], Aout[25], Aout[26], Aout[27], Aout[28], Aout[29], Aout[30], Aout[31]);
  not not_2 (Zero, or_3_out);

  assign sign = Aout[31];
endmodule

module comp4 (
  input  [3:0] A,
  input  [3:0] B,
  output A_eq_B,
  output A_gt_B
);

  wire and_2_out, comp2_1_a_eq_b, comp2_1_a_gt_b, comp2_2_a_eq_b, comp2_2_a_gt_b;

  comp2 comp2_1 (.A(A[3:2]), .B(B[3:2]), .A_gt_B(comp2_1_a_gt_b), .A_eq_B(comp2_1_a_eq_b));
  comp2 comp2_2 (.A(A[1:0]), .B(B[1:0]), .A_gt_B(comp2_2_a_gt_b), .A_eq_B(comp2_2_a_eq_b));
  and and_1 (A_eq_B, comp2_1_a_eq_b, comp2_2_a_eq_b);
  or or_1 (A_gt_B, comp2_1_a_gt_b, and_2_out);
  and and_2 (and_2_out, comp2_1_a_eq_b, comp2_2_a_gt_b);
endmodule

module comp1 (
  input  in_1,
  input  in_2,
  output A_gt_B,
  output A_eq_B
);

  and and_1 (A_gt_B, in_1, ~in_2);  // AND_Gate
  xnor xnor_1 (A_eq_B, in_2, in_1);
endmodule

module comp2 (
  input  [1:0] A,
  input  [1:0] B,
  output A_gt_B,
  output A_eq_B
);

  wire and_1_out, comp1_1_a_eq_b, comp1_1_a_gt_b, comp1_2_a_eq_b, comp1_2_a_gt_b;

  comp1 comp1_1 (.in_1(A[1]), .in_2(B[1]), .A_gt_B(comp1_1_a_gt_b), .A_eq_B(comp1_1_a_eq_b));
  comp1 comp1_2 (.in_1(A[0]), .in_2(B[0]), .A_gt_B(comp1_2_a_gt_b), .A_eq_B(comp1_2_a_eq_b));
  and and_1 (and_1_out, comp1_1_a_eq_b, comp1_2_a_gt_b);
  and and_2 (A_eq_B, comp1_1_a_eq_b, comp1_2_a_eq_b);
  or or_1 (A_gt_B, comp1_1_a_gt_b, and_1_out);
endmodule

module ha (
  input  A,
  input  B,
  output sum,
  output cout
);

  wire or_1_out;

  or or_1 (or_1_out, A, B);
  and and_1 (cout, A, B);
  and and_2 (sum, or_1_out, ~cout);  // AND_Gate
endmodule

module fa (
  input  A,
  input  B,
  input  cin,
  output sum,
  output cout
);

  wire ha_1_cout, ha_1_sum, ha_2_cout;

  ha ha_1 (.A(A), .B(B), .sum(ha_1_sum), .cout(ha_1_cout));
  ha ha_2 (.A(ha_1_sum), .B(cin), .sum(sum), .cout(ha_2_cout));
  or or_1 (cout, ha_2_cout, ha_1_cout);
endmodule

module comp8 (
  input  [7:0] A,
  input  [7:0] B,
  output A_eq_B,
  output A_gt_B
);

  wire and_1_out, comp4_1_a_eq_b, comp4_1_a_gt_b, comp4_2_a_eq_b, comp4_2_a_gt_b;

  comp4 comp4_1 (.A(A[7:4]), .B(B[7:4]), .A_eq_B(comp4_1_a_eq_b), .A_gt_B(comp4_1_a_gt_b));
  comp4 comp4_2 (.A(A[3:0]), .B(B[3:0]), .A_eq_B(comp4_2_a_eq_b), .A_gt_B(comp4_2_a_gt_b));
  and and_1 (and_1_out, comp4_1_a_eq_b, comp4_2_a_gt_b);
  and and_2 (A_eq_B, comp4_1_a_eq_b, comp4_2_a_eq_b);
  or or_1 (A_gt_B, comp4_1_a_gt_b, and_1_out);
endmodule

module comp16 (
  input  [15:0] A,
  input  [15:0] B,
  output A_eq_B,
  output A_gt_B
);

  wire and_1_out, comp8_1_a_eq_b, comp8_1_a_gt_b, comp8_2_a_eq_b, comp8_2_a_gt_b;

  comp8 comp8_1 (.A(A[15:8]), .B(B[15:8]), .A_eq_B(comp8_1_a_eq_b), .A_gt_B(comp8_1_a_gt_b));
  comp8 comp8_2 (.A(A[7:0]), .B(B[7:0]), .A_eq_B(comp8_2_a_eq_b), .A_gt_B(comp8_2_a_gt_b));
  or or_1 (A_gt_B, comp8_1_a_gt_b, and_1_out);
  and and_1 (and_1_out, comp8_1_a_eq_b, comp8_2_a_gt_b);
  and and_2 (A_eq_B, comp8_1_a_eq_b, comp8_2_a_eq_b);
endmodule

module add4_carry (
  input  C0,
  input  P0,
  input  G0,
  input  P1,
  input  G1,
  input  P2,
  input  G2,
  input  P3,
  input  G3,
  output C1,
  output C2,
  output C3,
  output C4,
  output P,
  output G
);

  wire and_1_out, and_2_out, and_3_out, and_4_out, and_5_out, and_6_out, and_7_out;

  and and_1 (and_1_out, C0, P0);
  or or_1 (C1, and_1_out, G0);
  and and_2 (and_2_out, C1, P1);
  or or_2 (C2, and_2_out, G1);
  and and_3 (and_3_out, G0, P2, P3, P1);
  and and_4 (and_4_out, C2, P2);
  or or_3 (C3, and_4_out, G2);
  and and_5 (and_5_out, G1, P2, P3);
  and and_6 (and_6_out, C3, P3);
  or or_4 (C4, and_6_out, G3);
  and and_7 (and_7_out, P3, G2);
  and and_8 (P, P0, P1, P2, P3);
  or or_5 (G, G3, and_7_out, and_5_out, and_3_out);
endmodule

module add4 (
  input  [3:0] A,
  input  [3:0] B,
  input  Cin,
  output [3:0] S,
  output Cout
);

  wire add4_carry_1_c1, add4_carry_1_c2, add4_carry_1_c3, add4_carry_1_g, add4_carry_1_p, and_1_out,
       fa_carry_1_g, fa_carry_1_p, fa_carry_2_g, fa_carry_2_p, fa_carry_3_g, fa_carry_3_p, fa_carry_4_g,
       fa_carry_4_p;

  fa_carry fa_carry_1 (.A(A[0]), .B(B[0]), .C(Cin), .S(S[0]), .P(fa_carry_1_p), .G(fa_carry_1_g));
  fa_carry fa_carry_2 (.A(A[1]), .B(B[1]), .C(add4_carry_1_c1), .S(S[1]), .P(fa_carry_2_p), .G(fa_carry_2_g));
  fa_carry fa_carry_3 (.A(A[2]), .B(B[2]), .C(add4_carry_1_c2), .S(S[2]), .P(fa_carry_3_p), .G(fa_carry_3_g));
  fa_carry fa_carry_4 (.A(A[3]), .B(B[3]), .C(add4_carry_1_c3), .S(S[3]), .P(fa_carry_4_p), .G(fa_carry_4_g));
  add4_carry add4_carry_1 (
    .G0(fa_carry_1_g), .P1(fa_carry_2_p), .G1(fa_carry_2_g), .P2(fa_carry_3_p), .G2(fa_carry_3_g),
    .P3(fa_carry_4_p), .G3(fa_carry_4_g), .C0(Cin), .P0(fa_carry_1_p), .C2(add4_carry_1_c2),
    .C3(add4_carry_1_c3), .C1(add4_carry_1_c1), .P(add4_carry_1_p), .G(add4_carry_1_g));  // open: C4
  and and_1 (and_1_out, add4_carry_1_p, Cin);
  or or_1 (Cout, and_1_out, add4_carry_1_g);
endmodule

module fa_carry (
  input  A,
  input  B,
  input  C,
  output S,
  output P,
  output G
);

  wire xor_1_out;

  xor xor_1 (xor_1_out, A, B);
  xor xor_2 (S, xor_1_out, C);
  or or_1 (P, A, B);
  and and_1 (G, A, B);
endmodule

module add8 (
  input  [7:0] A,
  input  [7:0] B,
  input  cin,
  output [7:0] S,
  output Cout
);

  wire add4_1_cout;

  add4 add4_1 (.A(A[3:0]), .B(B[3:0]), .Cin(cin), .S(S[3:0]), .Cout(add4_1_cout));
  add4 add4_2 (.A(A[7:4]), .B(B[7:4]), .Cin(add4_1_cout), .S(S[7:4]), .Cout(Cout));
endmodule

module add16 (
  input  [15:0] A,
  input  [15:0] B,
  input  Cin,
  output [15:0] S,
  output Cout
);

  wire add8_fast_1_cout;

  add8_fast add8_fast_1 (.A(A[7:0]), .B(B[7:0]), .Cin(Cin), .S(S[7:0]), .Cout(add8_fast_1_cout));
  add8_fast add8_fast_2 (.A(A[15:8]), .B(B[15:8]), .Cin(add8_fast_1_cout), .S(S[15:8]), .Cout(Cout));
endmodule

module add32 (
  input  [31:0] A,
  input  [31:0] B,
  input  Cin,
  output [31:0] S,
  output Cout
);

  wire add16_1_cout;

  add16 add16_1 (.A(A[15:0]), .B(B[15:0]), .Cin(Cin), .S(S[15:0]), .Cout(add16_1_cout));
  add16 add16_2 (.A(A[31:16]), .B(B[31:16]), .Cin(add16_1_cout), .S(S[31:16]), .Cout(Cout));
endmodule

module addsub32 (
  input  [31:0] A,
  input  [31:0] B,
  input  Cin,
  input  sub,
  output [31:0] S,
  output Cout
);

  wire or_1_out;
  wire [31:0] bit_extender_1_out, xor_1_out;

  or or_1 (or_1_out, Cin, sub);
  assign bit_extender_1_out = {{31{sub}}, sub};  // Bit_Extender bit_extender_1
  assign xor_1_out = B ^ bit_extender_1_out;  // XOR_Gate xor_1, 32 bits wide
  add32 add32_1 (.A(A), .B(xor_1_out), .Cin(or_1_out), .S(S), .Cout(Cout));
endmodule

module dec4 (
  input  [3:0] in_1,
  output out_2,
  output out_3,
  output out_4,
  output out_5,
  output out_6,
  output out_7,
  output out_8,
  output out_9,
  output out_10,
  output out_11,
  output out_12,
  output out_13,
  output out_14,
  output out_15,
  output out_16,
  output out_17
);

  wire not_1_out, not_2_out, not_3_out, not_4_out;

  not not_1 (not_1_out, in_1[3]);
  not not_2 (not_2_out, in_1[2]);
  not not_3 (not_3_out, in_1[1]);
  not not_4 (not_4_out, in_1[0]);
  and and_1 (out_2, not_4_out, not_3_out, not_2_out, not_1_out);
  and and_2 (out_3, in_1[0], not_3_out, not_2_out, not_1_out);
  and and_3 (out_4, not_4_out, in_1[1], not_2_out, not_1_out);
  and and_4 (out_5, in_1[0], in_1[1], not_2_out, not_1_out);
  and and_5 (out_6, not_4_out, not_3_out, in_1[2], not_1_out);
  and and_6 (out_7, in_1[0], not_3_out, in_1[2], not_1_out);
  and and_7 (out_8, not_4_out, in_1[1], in_1[2], not_1_out);
  and and_8 (out_9, in_1[0], in_1[1], in_1[2], not_1_out);
  and and_9 (out_10, not_4_out, not_3_out, not_2_out, in_1[3]);
  and and_10 (out_11, in_1[0], not_3_out, not_2_out, in_1[3]);
  and and_11 (out_12, not_4_out, in_1[1], not_2_out, in_1[3]);
  and and_12 (out_13, in_1[0], in_1[1], not_2_out, in_1[3]);
  and and_13 (out_14, not_4_out, not_3_out, in_1[2], in_1[3]);
  and and_14 (out_15, in_1[0], not_3_out, in_1[2], in_1[3]);
  and and_15 (out_16, not_4_out, in_1[1], in_1[2], in_1[3]);
  and and_16 (out_17, in_1[0], in_1[1], in_1[2], in_1[3]);
endmodule

module rising (
  input  in_1,
  output out_2
);

  wire not_1_out, not_2_out, not_3_out;

  not not_1 (not_1_out, in_1);
  not not_2 (not_2_out, not_1_out);
  not not_3 (not_3_out, not_2_out);
  and and_1 (out_2, in_1, not_3_out);
endmodule

module dlatch (
  input  D,
  input  E,
  input  reset,
  output Q,
  output nQ
);

  wire and_1_out, and_2_out, not_1_out, or_1_out;

  not not_1 (not_1_out, D);
  and and_1 (and_1_out, not_1_out, E);
  and and_2 (and_2_out, E, D);
  or or_1 (or_1_out, and_2_out, reset);
  nor nor_1 (Q, and_1_out, nQ);
  nor nor_2 (nQ, Q, or_1_out);
endmodule

module dflipflop (
  input  D,
  input  CLK,
  input  EN,
  input  O,
  output Q,
  output nQ
);

  wire and_1_out, dlatch_1_q, not_1_out;

  and and_1 (and_1_out, CLK, EN);
  not not_1 (not_1_out, and_1_out);
  dlatch dlatch_1 (.D(D), .E(and_1_out), .reset(O), .Q(dlatch_1_q));  // open: nQ
  dlatch dlatch_2 (.D(dlatch_1_q), .E(not_1_out), .reset(O), .Q(Q), .nQ(nQ));
endmodule

module add8_fast (
  input  [7:0] A,
  input  [7:0] B,
  input  Cin,
  output [7:0] S,
  output Cout
);

  wire and_1_out, C0P0P1_out, C0P0P1P2_out, C0P0P1P2P3_out, C0P0P1P2P3P4_out, C0P0P1P2P3P4P5_out,
       C0P0P1P2P3P4P5P6_out, G0P1_out, G0P1P2_out, G0P1P2P3_out, G0P1P2P3P4_out, G0P1P2P3P4P5_out,
       G0P1P2P3P4P5P6_out, G0P1P2P3P4P5P6P7_out, G1P2_out, G1P2P3_out, G1P2P3P4_out, G1P2P3P4P5_out,
       G1P2P3P4P5P6_out, G1P2P3P4P5P6P7_out, G2P3_out, G2P3P4_out, G2P3P4P5_out, G2P3P4P5P6_out,
       G2P3P4P5P6P7_out, G3P4_out, G3P4P5_out, G3P4P5P6_out, G3P4P5P6P7_out, G4P5_out, G4P5P6_out,
       G4P5P6P7_out, G5P6_out, G5P6P7_out, G6P7_out, P0C0_out;
  wire [7:0] ab8topg_1_g, ab8topg_1_p;
  wire [7:1] C1_out;

  AB8toPG ab8topg_1 (.A(A), .B(B), .P(ab8topg_1_p), .G(ab8topg_1_g));
  and P0C0 (P0C0_out, Cin, ab8topg_1_p[0]);
  or C1 (C1_out[1], P0C0_out, ab8topg_1_g[0]);
  and G0P1 (G0P1_out, ab8topg_1_g[0], ab8topg_1_p[1]);
  or C2 (C1_out[2], ab8topg_1_g[1], G0P1_out, C0P0P1_out);
  and C0P0P1 (C0P0P1_out, ab8topg_1_p[0], ab8topg_1_p[1], Cin);
  and G1P2 (G1P2_out, ab8topg_1_p[2], ab8topg_1_g[1]);
  and G0P1P2 (G0P1P2_out, ab8topg_1_p[1], ab8topg_1_p[2], ab8topg_1_g[0]);
  and C0P0P1P2 (C0P0P1P2_out, ab8topg_1_p[0], ab8topg_1_p[1], ab8topg_1_p[2], Cin);
  and G2P3 (G2P3_out, ab8topg_1_p[3], ab8topg_1_g[2]);
  and G1P2P3 (G1P2P3_out, ab8topg_1_p[2], ab8topg_1_p[3], ab8topg_1_g[1]);
  and G0P1P2P3 (G0P1P2P3_out, ab8topg_1_p[1], ab8topg_1_p[2], ab8topg_1_p[3], ab8topg_1_g[0]);
  and C0P0P1P2P3 (C0P0P1P2P3_out, ab8topg_1_p[0], ab8topg_1_p[1], ab8topg_1_p[2], ab8topg_1_p[3], Cin);
  and G3P4 (G3P4_out, ab8topg_1_p[4], ab8topg_1_g[3]);
  and G2P3P4 (G2P3P4_out, ab8topg_1_p[3], ab8topg_1_p[4], ab8topg_1_g[2]);
  and G1P2P3P4 (G1P2P3P4_out, ab8topg_1_p[2], ab8topg_1_p[3], ab8topg_1_p[4], ab8topg_1_g[1]);
  and G0P1P2P3P4 (G0P1P2P3P4_out, ab8topg_1_p[1], ab8topg_1_p[2], ab8topg_1_p[3], ab8topg_1_p[4], ab8topg_1_g[0]);
  and C0P0P1P2P3P4 (C0P0P1P2P3P4_out, ab8topg_1_p[0], ab8topg_1_p[1], ab8topg_1_p[2], ab8topg_1_p[3], ab8topg_1_p[4], Cin);
  and G4P5 (G4P5_out, ab8topg_1_p[5], ab8topg_1_g[4]);
  and G3P4P5 (G3P4P5_out, ab8topg_1_p[4], ab8topg_1_p[5], ab8topg_1_g[3]);
  and G2P3P4P5 (G2P3P4P5_out, ab8topg_1_p[3], ab8topg_1_p[4], ab8topg_1_p[5], ab8topg_1_g[2]);
  and G1P2P3P4P5 (G1P2P3P4P5_out, ab8topg_1_p[2], ab8topg_1_p[3], ab8topg_1_p[4], ab8topg_1_p[5], ab8topg_1_g[1]);
  and G0P1P2P3P4P5 (G0P1P2P3P4P5_out, ab8topg_1_p[1], ab8topg_1_p[2], ab8topg_1_p[3], ab8topg_1_p[4], ab8topg_1_p[5], ab8topg_1_g[0]);
  and C0P0P1P2P3P4P5 (C0P0P1P2P3P4P5_out, ab8topg_1_p[0], ab8topg_1_p[1], ab8topg_1_p[2], ab8topg_1_p[3], ab8topg_1_p[4], ab8topg_1_p[5], Cin);
  and G5P6 (G5P6_out, ab8topg_1_p[6], ab8topg_1_g[5]);
  and G4P5P6 (G4P5P6_out, ab8topg_1_p[5], ab8topg_1_p[6], ab8topg_1_g[4]);
  and G3P4P5P6 (G3P4P5P6_out, ab8topg_1_p[4], ab8topg_1_p[5], ab8topg_1_p[6], ab8topg_1_g[3]);
  and G2P3P4P5P6 (G2P3P4P5P6_out, ab8topg_1_p[3], ab8topg_1_p[4], ab8topg_1_p[5], ab8topg_1_p[6], ab8topg_1_g[2]);
  and G1P2P3P4P5P6 (G1P2P3P4P5P6_out, ab8topg_1_p[2], ab8topg_1_p[3], ab8topg_1_p[4], ab8topg_1_p[5], ab8topg_1_p[6], ab8topg_1_g[1]);
  and G0P1P2P3P4P5P6 (G0P1P2P3P4P5P6_out, ab8topg_1_p[1], ab8topg_1_p[2], ab8topg_1_p[3], ab8topg_1_p[4], ab8topg_1_p[5], ab8topg_1_p[6], ab8topg_1_g[0]);
  and C0P0P1P2P3P4P5P6 (C0P0P1P2P3P4P5P6_out, ab8topg_1_p[0], ab8topg_1_p[1], ab8topg_1_p[2], ab8topg_1_p[3], ab8topg_1_p[4], ab8topg_1_p[5], ab8topg_1_p[6], Cin);
  and G6P7 (G6P7_out, ab8topg_1_p[7], ab8topg_1_g[6]);
  and G5P6P7 (G5P6P7_out, ab8topg_1_p[6], ab8topg_1_p[7], ab8topg_1_g[5]);
  and G4P5P6P7 (G4P5P6P7_out, ab8topg_1_p[5], ab8topg_1_p[6], ab8topg_1_p[7], ab8topg_1_g[4]);
  and G3P4P5P6P7 (G3P4P5P6P7_out, ab8topg_1_p[4], ab8topg_1_p[5], ab8topg_1_p[6], ab8topg_1_p[7], ab8topg_1_g[3]);
  and G2P3P4P5P6P7 (G2P3P4P5P6P7_out, ab8topg_1_p[3], ab8topg_1_p[4], ab8topg_1_p[5], ab8topg_1_p[6], ab8topg_1_p[7], ab8topg_1_g[2]);
  and G1P2P3P4P5P6P7 (G1P2P3P4P5P6P7_out, ab8topg_1_p[2], ab8topg_1_p[4], ab8topg_1_p[5], ab8topg_1_p[3], ab8topg_1_p[6], ab8topg_1_p[7], ab8topg_1_g[1]);
  and G0P1P2P3P4P5P6P7 (G0P1P2P3P4P5P6P7_out, ab8topg_1_p[1], ab8topg_1_p[2], ab8topg_1_p[3], ab8topg_1_p[4], ab8topg_1_p[5], ab8topg_1_p[6], ab8topg_1_p[7], ab8topg_1_g[0]);
  and and_1 (and_1_out, ab8topg_1_p[0], ab8topg_1_p[1], ab8topg_1_p[2], ab8topg_1_p[3], ab8topg_1_p[4], ab8topg_1_p[5], ab8topg_1_p[6], ab8topg_1_p[7], Cin);
  or C3 (C1_out[3], ab8topg_1_g[2], G1P2_out, G0P1P2_out, C0P0P1P2_out);
  or C4 (C1_out[4], ab8topg_1_g[3], G2P3_out, G1P2P3_out, G0P1P2P3_out, C0P0P1P2P3_out);
  or C5 (C1_out[5], ab8topg_1_g[4], G3P4_out, G2P3P4_out, G1P2P3P4_out, G0P1P2P3P4_out, C0P0P1P2P3P4_out);
  or C6 (C1_out[6], ab8topg_1_g[5], G4P5_out, G3P4P5_out, G2P3P4P5_out, G1P2P3P4P5_out, G0P1P2P3P4P5_out, C0P0P1P2P3P4P5_out);
  or C7 (C1_out[7], ab8topg_1_g[6], G5P6_out, G4P5P6_out, G3P4P5P6_out, G2P3P4P5P6_out, G1P2P3P4P5P6_out, G0P1P2P3P4P5P6_out, C0P0P1P2P3P4P5P6_out);
  or C8 (Cout, ab8topg_1_g[7], G6P7_out, G5P6P7_out, G4P5P6P7_out, G3P4P5P6P7_out, G2P3P4P5P6P7_out, G1P2P3P4P5P6P7_out, G0P1P2P3P4P5P6P7_out, and_1_out);
  ABCtoS8 abctos8_1 (.A(A), .B(B), .C({C1_out, Cin}), .S(S));
endmodule

module ABtoPG (
  input  A,
  input  B,
  output P,
  output G
);

  or or_1 (P, A, B);
  and and_1 (G, A, B);
endmodule

module AB8toPG (
  input  [7:0] A,
  input  [7:0] B,
  output [7:0] P,
  output [7:0] G
);

  assign P = A | B;  // OR_Gate or_1, 8 bits wide
  assign G = A & B;  // AND_Gate and_1, 8 bits wide
endmodule

module ABCtoS (
  input  A,
  input  B,
  input  C,
  output S
);

  wire xor_1_out, xor_3_out;

  xor xor_1 (xor_1_out, A, B);
  xor xor_2 (S, xor_1_out, C);
  ExactlyOne xor_3 (.out(xor_3_out), .in0(A), .in1(B), .in2(C));
endmodule

module ABCtoS8 (
  input  [7:0] A,
  input  [7:0] B,
  input  [7:0] C,
  output [7:0] S
);

  wire [7:0] xor_1_out;

  assign xor_1_out = A ^ B;  // XOR_Gate xor_1, 8 bits wide
  assign S = xor_1_out ^ C;  // XOR_Gate xor_2, 8 bits wide
endmodule

module shr32 (
  input  [31:0] A,
  input  Cin,
  input  isRot,
  output [31:0] Aout,
  output Cout
);

  wire and_1_out, and_2_out;

  or or_1 (Aout[31], and_2_out, and_1_out);
  and and_1 (and_1_out, isRot, A[0]);
  and and_2 (and_2_out, Cin, ~isRot);  // AND_Gate

  assign Aout[30:0] = A[31:1];
  assign Cout = A[0];
endmodule

module shl32 (
  input  [31:0] A,
  input  Cin,
  input  isRot,
  output [31:0] Aout,
  output Cout
);

  wire and_1_out, and_2_out;

  or or_1 (Aout[0], and_2_out, and_1_out);
  and and_1 (and_1_out, isRot, A[31]);
  and and_2 (and_2_out, Cin, ~isRot);  // AND_Gate

  assign Aout[31:1] = A[30:0];
  assign Cout = A[31];
endmodule

module mux4x32 (
  input  [3:0] sel,
  input  [31:0] in_2,
  input  [31:0] in_3,
  input  [31:0] in_4,
  input  [31:0] in_5,
  input  [31:0] in_6,
  input  [31:0] in_7,
  input  [31:0] in_8,
  input  [31:0] in_9,
  input  [31:0] in_10,
  input  [31:0] in_11,
  input  [31:0] in_12,
  input  [31:0] in_13,
  input  [31:0] in_14,
  input  [31:0] in_15,
  input  [31:0] in_16,
  input  [31:0] in_17,
  output [31:0] out_18
);

  wire dec4_1_out_2, dec4_1_out_3, dec4_1_out_4, dec4_1_out_5, dec4_1_out_6, dec4_1_out_7, dec4_1_out_8,
       dec4_1_out_9, dec4_1_out_10, dec4_1_out_11, dec4_1_out_12, dec4_1_out_13, dec4_1_out_14,
       dec4_1_out_15, dec4_1_out_16, dec4_1_out_17;

  assign out_18 = dec4_1_out_16 ? in_16 : 32'bz;  // Controlled_Buffer controlled_buffer_1
  assign out_18 = dec4_1_out_17 ? in_17 : 32'bz;  // Controlled_Buffer controlled_buffer_2
  assign out_18 = dec4_1_out_12 ? in_12 : 32'bz;  // Controlled_Buffer controlled_buffer_3
  assign out_18 = dec4_1_out_13 ? in_13 : 32'bz;  // Controlled_Buffer controlled_buffer_4
  assign out_18 = dec4_1_out_14 ? in_14 : 32'bz;  // Controlled_Buffer controlled_buffer_5
  assign out_18 = dec4_1_out_15 ? in_15 : 32'bz;  // Controlled_Buffer controlled_buffer_6
  assign out_18 = dec4_1_out_8 ? in_8 : 32'bz;  // Controlled_Buffer controlled_buffer_7
  assign out_18 = dec4_1_out_9 ? in_9 : 32'bz;  // Controlled_Buffer controlled_buffer_8
  assign out_18 = dec4_1_out_10 ? in_10 : 32'bz;  // Controlled_Buffer controlled_buffer_9
  assign out_18 = dec4_1_out_11 ? in_11 : 32'bz;  // Controlled_Buffer controlled_buffer_10
  assign out_18 = dec4_1_out_4 ? in_4 : 32'bz;  // Controlled_Buffer controlled_buffer_11
  assign out_18 = dec4_1_out_5 ? in_5 : 32'bz;  // Controlled_Buffer controlled_buffer_12
  assign out_18 = dec4_1_out_6 ? in_6 : 32'bz;  // Controlled_Buffer controlled_buffer_13
  assign out_18 = dec4_1_out_7 ? in_7 : 32'bz;  // Controlled_Buffer controlled_buffer_14
  dec4 dec4_1 (
    .in_1(sel), .out_2(dec4_1_out_2), .out_3(dec4_1_out_3), .out_4(dec4_1_out_4), .out_5(dec4_1_out_5),
    .out_6(dec4_1_out_6), .out_7(dec4_1_out_7), .out_8(dec4_1_out_8), .out_9(dec4_1_out_9),
    .out_10(dec4_1_out_10), .out_11(dec4_1_out_11), .out_12(dec4_1_out_12), .out_13(dec4_1_out_13),
    .out_14(dec4_1_out_14), .out_15(dec4_1_out_15), .out_16(dec4_1_out_16), .out_17(dec4_1_out_17));
  assign out_18 = dec4_1_out_2 ? in_2 : 32'bz;  // Controlled_Buffer controlled_buffer_15
  assign out_18 = dec4_1_out_3 ? in_3 : 32'bz;  // Controlled_Buffer controlled_buffer_16
endmodule

module mux4x1 (
  input  [3:0] sel,
  input  in_2,
  input  in_3,
  input  in_4,
  input  in_5,
  input  in_6,
  input  in_7,
  input  in_8,
  input  in_9,
  input  in_10,
  input  in_11,
  input  in_12,
  input  in_13,
  input  in_14,
  input  in_15,
  input  in_16,
  input  in_17,
  output out_18
);

  wire dec4_1_out_2, dec4_1_out_3, dec4_1_out_4, dec4_1_out_5, dec4_1_out_6, dec4_1_out_7, dec4_1_out_8,
       dec4_1_out_9, dec4_1_out_10, dec4_1_out_11, dec4_1_out_12, dec4_1_out_13, dec4_1_out_14,
       dec4_1_out_15, dec4_1_out_16, dec4_1_out_17;

  assign out_18 = dec4_1_out_16 ? in_16 : 1'bz;  // Controlled_Buffer controlled_buffer_1
  assign out_18 = dec4_1_out_17 ? in_17 : 1'bz;  // Controlled_Buffer controlled_buffer_2
  assign out_18 = dec4_1_out_12 ? in_12 : 1'bz;  // Controlled_Buffer controlled_buffer_3
  assign out_18 = dec4_1_out_13 ? in_13 : 1'bz;  // Controlled_Buffer controlled_buffer_4
  assign out_18 = dec4_1_out_14 ? in_14 : 1'bz;  // Controlled_Buffer controlled_buffer_5
  assign out_18 = dec4_1_out_15 ? in_15 : 1'bz;  // Controlled_Buffer controlled_buffer_6
  assign out_18 = dec4_1_out_8 ? in_8 : 1'bz;  // Controlled_Buffer controlled_buffer_7
  assign out_18 = dec4_1_out_9 ? in_9 : 1'bz;  // Controlled_Buffer controlled_buffer_8
  assign out_18 = dec4_1_out_10 ? in_10 : 1'bz;  // Controlled_Buffer controlled_buffer_9
  assign out_18 = dec4_1_out_11 ? in_11 : 1'bz;  // Controlled_Buffer controlled_buffer_10
  assign out_18 = dec4_1_out_4 ? in_4 : 1'bz;  // Controlled_Buffer controlled_buffer_11
  assign out_18 = dec4_1_out_5 ? in_5 : 1'bz;  // Controlled_Buffer controlled_buffer_12
  assign out_18 = dec4_1_out_6 ? in_6 : 1'bz;  // Controlled_Buffer controlled_buffer_13
  assign out_18 = dec4_1_out_7 ? in_7 : 1'bz;  // Controlled_Buffer controlled_buffer_14
  dec4 dec4_1 (
    .in_1(sel), .out_2(dec4_1_out_2), .out_3(dec4_1_out_3), .out_4(dec4_1_out_4), .out_5(dec4_1_out_5),
    .out_6(dec4_1_out_6), .out_7(dec4_1_out_7), .out_8(dec4_1_out_8), .out_9(dec4_1_out_9),
    .out_10(dec4_1_out_10), .out_11(dec4_1_out_11), .out_12(dec4_1_out_12), .out_13(dec4_1_out_13),
    .out_14(dec4_1_out_14), .out_15(dec4_1_out_15), .out_16(dec4_1_out_16), .out_17(dec4_1_out_17));
  assign out_18 = dec4_1_out_2 ? in_2 : 1'bz;  // Controlled_Buffer controlled_buffer_15
  assign out_18 = dec4_1_out_3 ? in_3 : 1'bz;  // Controlled_Buffer controlled_buffer_16
endmodule

module mul4 (
  input  [3:0] in_1,
  input  [3:0] in_2,
  output [7:0] out_3
);

  wire [3:0] and_1_out, and_2_out, and_3_out, and_4_out, bit_extender_1_out, bit_extender_2_out,
       bit_extender_3_out, bit_extender_4_out;
  wire [7:0] adder_1_out, adder_2_out, bit_extender_5_out, bit_extender_6_out, bit_extender_7_out,
       bit_extender_8_out, mul4shl8_1_out_2, mul4shl8_2_out_2, mul4shl8_3_out_2, mul4shl8_4_out_2,
       mul4shl8_5_out_2, mul4shl8_6_out_2;

  assign bit_extender_1_out = {{3{in_1[0]}}, in_1[0]};  // Bit_Extender bit_extender_1
  assign bit_extender_2_out = {{3{in_1[1]}}, in_1[1]};  // Bit_Extender bit_extender_2
  assign bit_extender_3_out = {{3{in_1[2]}}, in_1[2]};  // Bit_Extender bit_extender_3
  assign bit_extender_4_out = {{3{in_1[3]}}, in_1[3]};  // Bit_Extender bit_extender_4
  assign bit_extender_5_out = {{4{1'b0}}, and_1_out};  // Bit_Extender bit_extender_5
  assign and_1_out = in_2 & bit_extender_1_out;  // AND_Gate and_1, 4 bits wide
  assign bit_extender_6_out = {{4{1'b0}}, and_2_out};  // Bit_Extender bit_extender_6
  assign and_2_out = in_2 & bit_extender_2_out;  // AND_Gate and_2, 4 bits wide
  assign bit_extender_7_out = {{4{1'b0}}, and_3_out};  // Bit_Extender bit_extender_7
  assign and_3_out = in_2 & bit_extender_3_out;  // AND_Gate and_3, 4 bits wide
  assign bit_extender_8_out = {{4{1'b0}}, and_4_out};  // Bit_Extender bit_extender_8
  assign and_4_out = in_2 & bit_extender_4_out;  // AND_Gate and_4, 4 bits wide
  mul4shl8 mul4shl8_1 (.in_1(bit_extender_6_out), .out_2(mul4shl8_1_out_2));
  mul4shl8 mul4shl8_2 (.in_1(bit_extender_7_out), .out_2(mul4shl8_2_out_2));
  mul4shl8 mul4shl8_3 (.in_1(bit_extender_8_out), .out_2(mul4shl8_3_out_2));
  Adder adder_1 (.a(bit_extender_5_out), .b(mul4shl8_1_out_2), .out(adder_1_out), .cin(1'b0));  // open: cout
  mul4shl8 mul4shl8_4 (.in_1(mul4shl8_2_out_2), .out_2(mul4shl8_4_out_2));
  mul4shl8 mul4shl8_5 (.in_1(mul4shl8_3_out_2), .out_2(mul4shl8_5_out_2));
  Adder adder_2 (.a(adder_1_out), .b(mul4shl8_4_out_2), .out(adder_2_out), .cin(1'b0));  // open: cout
  mul4shl8 mul4shl8_6 (.in_1(mul4shl8_5_out_2), .out_2(mul4shl8_6_out_2));
  Adder adder_3 (.a(adder_2_out), .b(mul4shl8_6_out_2), .out(out_3), .cin(1'b0));  // open: cout
endmodule

module mul4shl8 (
  input  [7:0] in_1,
  output [7:0] out_2
);


  assign out_2 = {in_1[6:0], in_1[7]};
endmodule

module mul16 (
  input  [15:0] A,
  input  [15:0] B,
  output [15:0] Lout,
  output [15:0] Hout
);

  wire adder_1_cout, adder_2_cout, adder_3_cout, adder_4_cout, adder_5_cout, adder_6_cout, adder_7_cout,
       adder_8_cout, adder_9_cout, adder_10_cout, adder_11_cout, adder_12_cout, adder_13_cout, adder_14_cout;
  wire [15:0] and_1_out, and_2_out, and_3_out, and_4_out, and_5_out, and_6_out, and_7_out, and_8_out,
       and_9_out, and_10_out, and_11_out, and_12_out, and_13_out, and_14_out, and_15_out, and_16_out,
       bit_extender_1_out, bit_extender_2_out, bit_extender_3_out, bit_extender_4_out, bit_extender_5_out,
       bit_extender_6_out, bit_extender_7_out, bit_extender_8_out, bit_extender_9_out, bit_extender_10_out,
       bit_extender_11_out, bit_extender_12_out, bit_extender_13_out, bit_extender_14_out,
       bit_extender_15_out, bit_extender_16_out;
  wire [31:0] adder_1_out, adder_2_out, adder_3_out, adder_4_out, adder_5_out, adder_6_out, adder_7_out,
       adder_8_out, adder_9_out, adder_10_out, adder_11_out, adder_12_out, adder_13_out, adder_14_out,
       bit_extender_17_out, bit_extender_18_out, bit_extender_19_out, bit_extender_20_out,
       bit_extender_21_out, bit_extender_22_out, bit_extender_23_out, bit_extender_24_out,
       bit_extender_25_out, bit_extender_26_out, bit_extender_27_out, bit_extender_28_out,
       bit_extender_29_out, bit_extender_30_out, bit_extender_31_out, bit_extender_32_out,
       mul16shl32_1_out_2, mul16shl32_2_out_2, mul16shl32_3_out_2, mul16shl32_4_out_2, mul16shl32_5_out_2,
       mul16shl32_6_out_2, mul16shl32_7_out_2, mul16shl32_8_out_2, mul16shl32_9_out_2, mul16shl32_10_out_2,
       mul16shl32_11_out_2, mul16shl32_12_out_2, mul16shl32_13_out_2, mul16shl32_14_out_2,
       mul16shl32_15_out_2, mul16shl32_16_out_2, mul16shl32_17_out_2, mul16shl32_18_out_2,
       mul16shl32_19_out_2, mul16shl32_20_out_2, mul16shl32_21_out_2, mul16shl32_22_out_2,
       mul16shl32_23_out_2, mul16shl32_24_out_2, mul16shl32_25_out_2, mul16shl32_26_out_2,
       mul16shl32_27_out_2, mul16shl32_28_out_2, mul16shl32_29_out_2, mul16shl32_30_out_2,
       mul16shl32_31_out_2, mul16shl32_32_out_2, mul16shl32_33_out_2, mul16shl32_34_out_2,
       mul16shl32_35_out_2, mul16shl32_36_out_2, mul16shl32_37_out_2, mul16shl32_38_out_2,
       mul16shl32_39_out_2, mul16shl32_40_out_2, mul16shl32_41_out_2, mul16shl32_42_out_2,
       mul16shl32_43_out_2, mul16shl32_44_out_2, mul16shl32_45_out_2, mul16shl32_46_out_2,
       mul16shl32_47_out_2, mul16shl32_48_out_2, mul16shl32_49_out_2, mul16shl32_50_out_2,
       mul16shl32_51_out_2, mul16shl32_52_out_2, mul16shl32_53_out_2, mul16shl32_54_out_2,
       mul16shl32_55_out_2, mul16shl32_56_out_2, mul16shl32_57_out_2, mul16shl32_58_out_2,
       mul16shl32_59_out_2, mul16shl32_60_out_2, mul16shl32_61_out_2, mul16shl32_62_out_2,
       mul16shl32_63_out_2, mul16shl32_64_out_2, mul16shl32_65_out_2, mul16shl32_66_out_2,
       mul16shl32_67_out_2, mul16shl32_68_out_2, mul16shl32_69_out_2, mul16shl32_70_out_2,
       mul16shl32_71_out_2, mul16shl32_72_out_2, mul16shl32_73_out_2, mul16shl32_74_out_2,
       mul16shl32_75_out_2, mul16shl32_76_out_2, mul16shl32_77_out_2, mul16shl32_78_out_2,
       mul16shl32_79_out_2, mul16shl32_80_out_2, mul16shl32_81_out_2, mul16shl32_82_out_2,
       mul16shl32_83_out_2, mul16shl32_84_out_2, mul16shl32_85_out_2, mul16shl32_86_out_2,
       mul16shl32_87_out_2, mul16shl32_88_out_2, mul16shl32_89_out_2, mul16shl32_90_out_2,
       mul16shl32_91_out_2, mul16shl32_92_out_2, mul16shl32_93_out_2, mul16shl32_94_out_2,
       mul16shl32_95_out_2, mul16shl32_96_out_2, mul16shl32_97_out_2, mul16shl32_98_out_2,
       mul16shl32_99_out_2, mul16shl32_100_out_2, mul16shl32_101_out_2, mul16shl32_102_out_2,
       mul16shl32_103_out_2, mul16shl32_104_out_2, mul16shl32_105_out_2, mul16shl32_106_out_2,
       mul16shl32_107_out_2, mul16shl32_108_out_2, mul16shl32_109_out_2, mul16shl32_110_out_2,
       mul16shl32_111_out_2, mul16shl32_112_out_2, mul16shl32_113_out_2, mul16shl32_114_out_2,
       mul16shl32_115_out_2, mul16shl32_116_out_2, mul16shl32_117_out_2, mul16shl32_118_out_2,
       mul16shl32_119_out_2, mul16shl32_120_out_2;

  assign bit_extender_1_out = {{15{A[0]}}, A[0]};  // Bit_Extender bit_extender_1
  assign bit_extender_2_out = {{15{A[1]}}, A[1]};  // Bit_Extender bit_extender_2
  assign bit_extender_3_out = {{15{A[2]}}, A[2]};  // Bit_Extender bit_extender_3
  assign bit_extender_4_out = {{15{A[3]}}, A[3]};  // Bit_Extender bit_extender_4
  assign bit_extender_5_out = {{15{A[4]}}, A[4]};  // Bit_Extender bit_extender_5
  assign bit_extender_6_out = {{15{A[5]}}, A[5]};  // Bit_Extender bit_extender_6
  assign bit_extender_7_out = {{15{A[6]}}, A[6]};  // Bit_Extender bit_extender_7
  assign bit_extender_8_out = {{15{A[7]}}, A[7]};  // Bit_Extender bit_extender_8
  assign bit_extender_9_out = {{15{A[8]}}, A[8]};  // Bit_Extender bit_extender_9
  assign bit_extender_10_out = {{15{A[9]}}, A[9]};  // Bit_Extender bit_extender_10
  assign bit_extender_11_out = {{15{A[10]}}, A[10]};  // Bit_Extender bit_extender_11
  assign bit_extender_12_out = {{15{A[11]}}, A[11]};  // Bit_Extender bit_extender_12
  assign bit_extender_13_out = {{15{A[12]}}, A[12]};  // Bit_Extender bit_extender_13
  assign bit_extender_14_out = {{15{A[13]}}, A[13]};  // Bit_Extender bit_extender_14
  assign bit_extender_15_out = {{15{A[14]}}, A[14]};  // Bit_Extender bit_extender_15
  assign bit_extender_16_out = {{15{A[15]}}, A[15]};  // Bit_Extender bit_extender_16
  assign and_1_out = B & bit_extender_1_out;  // AND_Gate and_1, 16 bits wide
  assign and_2_out = B & bit_extender_2_out;  // AND_Gate and_2, 16 bits wide
  assign and_3_out = B & bit_extender_3_out;  // AND_Gate and_3, 16 bits wide
  assign and_4_out = B & bit_extender_4_out;  // AND_Gate and_4, 16 bits wide
  assign and_5_out = B & bit_extender_5_out;  // AND_Gate and_5, 16 bits wide
  assign and_6_out = B & bit_extender_6_out;  // AND_Gate and_6, 16 bits wide
  assign and_7_out = B & bit_extender_7_out;  // AND_Gate and_7, 16 bits wide
  assign and_8_out = B & bit_extender_8_out;  // AND_Gate and_8, 16 bits wide
  assign and_9_out = B & bit_extender_9_out;  // AND_Gate and_9, 16 bits wide
  assign and_10_out = B & bit_extender_10_out;  // AND_Gate and_10, 16 bits wide
  assign and_11_out = B & bit_extender_11_out;  // AND_Gate and_11, 16 bits wide
  assign and_12_out = B & bit_extender_12_out;  // AND_Gate and_12, 16 bits wide
  assign and_13_out = B & bit_extender_13_out;  // AND_Gate and_13, 16 bits wide
  assign and_14_out = B & bit_extender_14_out;  // AND_Gate and_14, 16 bits wide
  assign and_15_out = B & bit_extender_15_out;  // AND_Gate and_15, 16 bits wide
  assign and_16_out = B & bit_extender_16_out;  // AND_Gate and_16, 16 bits wide
  assign bit_extender_17_out = {{16{1'b0}}, and_1_out};  // Bit_Extender bit_extender_17
  assign bit_extender_18_out = {{16{1'b0}}, and_2_out};  // Bit_Extender bit_extender_18
  assign bit_extender_19_out = {{16{1'b0}}, and_3_out};  // Bit_Extender bit_extender_19
  assign bit_extender_20_out = {{16{1'b0}}, and_4_out};  // Bit_Extender bit_extender_20
  assign bit_extender_21_out = {{16{1'b0}}, and_5_out};  // Bit_Extender bit_extender_21
  assign bit_extender_22_out = {{16{1'b0}}, and_6_out};  // Bit_Extender bit_extender_22
  assign bit_extender_23_out = {{16{1'b0}}, and_7_out};  // Bit_Extender bit_extender_23
  assign bit_extender_24_out = {{16{1'b0}}, and_8_out};  // Bit_Extender bit_extender_24
  assign bit_extender_25_out = {{16{1'b0}}, and_9_out};  // Bit_Extender bit_extender_25
  assign bit_extender_26_out = {{16{1'b0}}, and_10_out};  // Bit_Extender bit_extender_26
  assign bit_extender_27_out = {{16{1'b0}}, and_11_out};  // Bit_Extender bit_extender_27
  assign bit_extender_28_out = {{16{1'b0}}, and_12_out};  // Bit_Extender bit_extender_28
  assign bit_extender_29_out = {{16{1'b0}}, and_13_out};  // Bit_Extender bit_extender_29
  assign bit_extender_30_out = {{16{1'b0}}, and_14_out};  // Bit_Extender bit_extender_30
  assign bit_extender_31_out = {{16{1'b0}}, and_15_out};  // Bit_Extender bit_extender_31
  assign bit_extender_32_out = {{16{1'b0}}, and_16_out};  // Bit_Extender bit_extender_32
  mul16shl32 mul16shl32_1 (.in_1(bit_extender_18_out), .out_2(mul16shl32_1_out_2));
  mul16shl32 mul16shl32_2 (.in_1(bit_extender_19_out), .out_2(mul16shl32_2_out_2));
  mul16shl32 mul16shl32_3 (.in_1(bit_extender_20_out), .out_2(mul16shl32_3_out_2));
  mul16shl32 mul16shl32_4 (.in_1(bit_extender_21_out), .out_2(mul16shl32_4_out_2));
  mul16shl32 mul16shl32_5 (.in_1(bit_extender_22_out), .out_2(mul16shl32_5_out_2));
  mul16shl32 mul16shl32_6 (.in_1(bit_extender_23_out), .out_2(mul16shl32_6_out_2));
  mul16shl32 mul16shl32_7 (.in_1(bit_extender_24_out), .out_2(mul16shl32_7_out_2));
  mul16shl32 mul16shl32_8 (.in_1(bit_extender_25_out), .out_2(mul16shl32_8_out_2));
  mul16shl32 mul16shl32_9 (.in_1(bit_extender_26_out), .out_2(mul16shl32_9_out_2));
  mul16shl32 mul16shl32_10 (.in_1(bit_extender_27_out), .out_2(mul16shl32_10_out_2));
  mul16shl32 mul16shl32_11 (.in_1(bit_extender_28_out), .out_2(mul16shl32_11_out_2));
  mul16shl32 mul16shl32_12 (.in_1(bit_extender_29_out), .out_2(mul16shl32_12_out_2));
  mul16shl32 mul16shl32_13 (.in_1(bit_extender_30_out), .out_2(mul16shl32_13_out_2));
  mul16shl32 mul16shl32_14 (.in_1(bit_extender_31_out), .out_2(mul16shl32_14_out_2));
  mul16shl32 mul16shl32_15 (.in_1(bit_extender_32_out), .out_2(mul16shl32_15_out_2));
  Adder #(.width(32)) adder_1 (
    .a(bit_extender_17_out), .b(mul16shl32_1_out_2), .out(adder_1_out), .cin(1'b0), .cout(adder_1_cout));
  mul16shl32 mul16shl32_16 (.in_1(mul16shl32_2_out_2), .out_2(mul16shl32_16_out_2));
  mul16shl32 mul16shl32_17 (.in_1(mul16shl32_3_out_2), .out_2(mul16shl32_17_out_2));
  mul16shl32 mul16shl32_18 (.in_1(mul16shl32_4_out_2), .out_2(mul16shl32_18_out_2));
  mul16shl32 mul16shl32_19 (.in_1(mul16shl32_5_out_2), .out_2(mul16shl32_19_out_2));
  mul16shl32 mul16shl32_20 (.in_1(mul16shl32_6_out_2), .out_2(mul16shl32_20_out_2));
  mul16shl32 mul16shl32_21 (.in_1(mul16shl32_7_out_2), .out_2(mul16shl32_21_out_2));
  mul16shl32 mul16shl32_22 (.in_1(mul16shl32_8_out_2), .out_2(mul16shl32_22_out_2));
  mul16shl32 mul16shl32_23 (.in_1(mul16shl32_9_out_2), .out_2(mul16shl32_23_out_2));
  mul16shl32 mul16shl32_24 (.in_1(mul16shl32_10_out_2), .out_2(mul16shl32_24_out_2));
  mul16shl32 mul16shl32_25 (.in_1(mul16shl32_11_out_2), .out_2(mul16shl32_25_out_2));
  mul16shl32 mul16shl32_26 (.in_1(mul16shl32_12_out_2), .out_2(mul16shl32_26_out_2));
  mul16shl32 mul16shl32_27 (.in_1(mul16shl32_13_out_2), .out_2(mul16shl32_27_out_2));
  mul16shl32 mul16shl32_28 (.in_1(mul16shl32_14_out_2), .out_2(mul16shl32_28_out_2));
  mul16shl32 mul16shl32_29 (.in_1(mul16shl32_15_out_2), .out_2(mul16shl32_29_out_2));
  Adder #(.width(32)) adder_2 (
    .a(adder_1_out), .b(mul16shl32_16_out_2), .out(adder_2_out), .cin(adder_1_cout), .cout(adder_2_cout));
  mul16shl32 mul16shl32_30 (.in_1(mul16shl32_17_out_2), .out_2(mul16shl32_30_out_2));
  mul16shl32 mul16shl32_31 (.in_1(mul16shl32_18_out_2), .out_2(mul16shl32_31_out_2));
  mul16shl32 mul16shl32_32 (.in_1(mul16shl32_19_out_2), .out_2(mul16shl32_32_out_2));
  mul16shl32 mul16shl32_33 (.in_1(mul16shl32_20_out_2), .out_2(mul16shl32_33_out_2));
  mul16shl32 mul16shl32_34 (.in_1(mul16shl32_21_out_2), .out_2(mul16shl32_34_out_2));
  mul16shl32 mul16shl32_35 (.in_1(mul16shl32_22_out_2), .out_2(mul16shl32_35_out_2));
  mul16shl32 mul16shl32_36 (.in_1(mul16shl32_23_out_2), .out_2(mul16shl32_36_out_2));
  mul16shl32 mul16shl32_37 (.in_1(mul16shl32_24_out_2), .out_2(mul16shl32_37_out_2));
  mul16shl32 mul16shl32_38 (.in_1(mul16shl32_25_out_2), .out_2(mul16shl32_38_out_2));
  mul16shl32 mul16shl32_39 (.in_1(mul16shl32_26_out_2), .out_2(mul16shl32_39_out_2));
  mul16shl32 mul16shl32_40 (.in_1(mul16shl32_27_out_2), .out_2(mul16shl32_40_out_2));
  mul16shl32 mul16shl32_41 (.in_1(mul16shl32_28_out_2), .out_2(mul16shl32_41_out_2));
  mul16shl32 mul16shl32_42 (.in_1(mul16shl32_29_out_2), .out_2(mul16shl32_42_out_2));
  Adder #(.width(32)) adder_3 (
    .a(adder_2_out), .b(mul16shl32_30_out_2), .out(adder_3_out), .cin(adder_2_cout), .cout(adder_3_cout));
  mul16shl32 mul16shl32_43 (.in_1(mul16shl32_31_out_2), .out_2(mul16shl32_43_out_2));
  mul16shl32 mul16shl32_44 (.in_1(mul16shl32_32_out_2), .out_2(mul16shl32_44_out_2));
  mul16shl32 mul16shl32_45 (.in_1(mul16shl32_33_out_2), .out_2(mul16shl32_45_out_2));
  mul16shl32 mul16shl32_46 (.in_1(mul16shl32_34_out_2), .out_2(mul16shl32_46_out_2));
  mul16shl32 mul16shl32_47 (.in_1(mul16shl32_35_out_2), .out_2(mul16shl32_47_out_2));
  mul16shl32 mul16shl32_48 (.in_1(mul16shl32_36_out_2), .out_2(mul16shl32_48_out_2));
  mul16shl32 mul16shl32_49 (.in_1(mul16shl32_37_out_2), .out_2(mul16shl32_49_out_2));
  mul16shl32 mul16shl32_50 (.in_1(mul16shl32_38_out_2), .out_2(mul16shl32_50_out_2));
  mul16shl32 mul16shl32_51 (.in_1(mul16shl32_39_out_2), .out_2(mul16shl32_51_out_2));
  mul16shl32 mul16shl32_52 (.in_1(mul16shl32_40_out_2), .out_2(mul16shl32_52_out_2));
  mul16shl32 mul16shl32_53 (.in_1(mul16shl32_41_out_2), .out_2(mul16shl32_53_out_2));
  mul16shl32 mul16shl32_54 (.in_1(mul16shl32_42_out_2), .out_2(mul16shl32_54_out_2));
  Adder #(.width(32)) adder_4 (
    .a(adder_3_out), .b(mul16shl32_43_out_2), .out(adder_4_out), .cin(adder_3_cout), .cout(adder_4_cout));
  mul16shl32 mul16shl32_55 (.in_1(mul16shl32_44_out_2), .out_2(mul16shl32_55_out_2));
  mul16shl32 mul16shl32_56 (.in_1(mul16shl32_45_out_2), .out_2(mul16shl32_56_out_2));
  mul16shl32 mul16shl32_57 (.in_1(mul16shl32_46_out_2), .out_2(mul16shl32_57_out_2));
  mul16shl32 mul16shl32_58 (.in_1(mul16shl32_47_out_2), .out_2(mul16shl32_58_out_2));
  mul16shl32 mul16shl32_59 (.in_1(mul16shl32_48_out_2), .out_2(mul16shl32_59_out_2));
  mul16shl32 mul16shl32_60 (.in_1(mul16shl32_49_out_2), .out_2(mul16shl32_60_out_2));
  mul16shl32 mul16shl32_61 (.in_1(mul16shl32_50_out_2), .out_2(mul16shl32_61_out_2));
  mul16shl32 mul16shl32_62 (.in_1(mul16shl32_51_out_2), .out_2(mul16shl32_62_out_2));
  mul16shl32 mul16shl32_63 (.in_1(mul16shl32_52_out_2), .out_2(mul16shl32_63_out_2));
  mul16shl32 mul16shl32_64 (.in_1(mul16shl32_53_out_2), .out_2(mul16shl32_64_out_2));
  mul16shl32 mul16shl32_65 (.in_1(mul16shl32_54_out_2), .out_2(mul16shl32_65_out_2));
  Adder #(.width(32)) adder_5 (
    .a(adder_4_out), .b(mul16shl32_55_out_2), .out(adder_5_out), .cin(adder_4_cout), .cout(adder_5_cout));
  mul16shl32 mul16shl32_66 (.in_1(mul16shl32_56_out_2), .out_2(mul16shl32_66_out_2));
  mul16shl32 mul16shl32_67 (.in_1(mul16shl32_57_out_2), .out_2(mul16shl32_67_out_2));
  mul16shl32 mul16shl32_68 (.in_1(mul16shl32_58_out_2), .out_2(mul16shl32_68_out_2));
  mul16shl32 mul16shl32_69 (.in_1(mul16shl32_59_out_2), .out_2(mul16shl32_69_out_2));
  mul16shl32 mul16shl32_70 (.in_1(mul16shl32_60_out_2), .out_2(mul16shl32_70_out_2));
  mul16shl32 mul16shl32_71 (.in_1(mul16shl32_61_out_2), .out_2(mul16shl32_71_out_2));
  mul16shl32 mul16shl32_72 (.in_1(mul16shl32_62_out_2), .out_2(mul16shl32_72_out_2));
  mul16shl32 mul16shl32_73 (.in_1(mul16shl32_63_out_2), .out_2(mul16shl32_73_out_2));
  mul16shl32 mul16shl32_74 (.in_1(mul16shl32_64_out_2), .out_2(mul16shl32_74_out_2));
  mul16shl32 mul16shl32_75 (.in_1(mul16shl32_65_out_2), .out_2(mul16shl32_75_out_2));
  Adder #(.width(32)) adder_6 (
    .a(adder_5_out), .b(mul16shl32_66_out_2), .out(adder_6_out), .cin(adder_5_cout), .cout(adder_6_cout));
  mul16shl32 mul16shl32_76 (.in_1(mul16shl32_67_out_2), .out_2(mul16shl32_76_out_2));
  mul16shl32 mul16shl32_77 (.in_1(mul16shl32_68_out_2), .out_2(mul16shl32_77_out_2));
  mul16shl32 mul16shl32_78 (.in_1(mul16shl32_69_out_2), .out_2(mul16shl32_78_out_2));
  mul16shl32 mul16shl32_79 (.in_1(mul16shl32_70_out_2), .out_2(mul16shl32_79_out_2));
  mul16shl32 mul16shl32_80 (.in_1(mul16shl32_71_out_2), .out_2(mul16shl32_80_out_2));
  mul16shl32 mul16shl32_81 (.in_1(mul16shl32_72_out_2), .out_2(mul16shl32_81_out_2));
  mul16shl32 mul16shl32_82 (.in_1(mul16shl32_73_out_2), .out_2(mul16shl32_82_out_2));
  mul16shl32 mul16shl32_83 (.in_1(mul16shl32_74_out_2), .out_2(mul16shl32_83_out_2));
  mul16shl32 mul16shl32_84 (.in_1(mul16shl32_75_out_2), .out_2(mul16shl32_84_out_2));
  Adder #(.width(32)) adder_7 (
    .a(adder_6_out), .b(mul16shl32_76_out_2), .out(adder_7_out), .cin(adder_6_cout), .cout(adder_7_cout));
  mul16shl32 mul16shl32_85 (.in_1(mul16shl32_77_out_2), .out_2(mul16shl32_85_out_2));
  mul16shl32 mul16shl32_86 (.in_1(mul16shl32_78_out_2), .out_2(mul16shl32_86_out_2));
  mul16shl32 mul16shl32_87 (.in_1(mul16shl32_79_out_2), .out_2(mul16shl32_87_out_2));
  mul16shl32 mul16shl32_88 (.in_1(mul16shl32_80_out_2), .out_2(mul16shl32_88_out_2));
  mul16shl32 mul16shl32_89 (.in_1(mul16shl32_81_out_2), .out_2(mul16shl32_89_out_2));
  mul16shl32 mul16shl32_90 (.in_1(mul16shl32_82_out_2), .out_2(mul16shl32_90_out_2));
  mul16shl32 mul16shl32_91 (.in_1(mul16shl32_83_out_2), .out_2(mul16shl32_91_out_2));
  mul16shl32 mul16shl32_92 (.in_1(mul16shl32_84_out_2), .out_2(mul16shl32_92_out_2));
  Adder #(.width(32)) adder_8 (
    .a(adder_7_out), .b(mul16shl32_85_out_2), .out(adder_8_out), .cin(adder_7_cout), .cout(adder_8_cout));
  mul16shl32 mul16shl32_93 (.in_1(mul16shl32_86_out_2), .out_2(mul16shl32_93_out_2));
  mul16shl32 mul16shl32_94 (.in_1(mul16shl32_87_out_2), .out_2(mul16shl32_94_out_2));
  mul16shl32 mul16shl32_95 (.in_1(mul16shl32_88_out_2), .out_2(mul16shl32_95_out_2));
  mul16shl32 mul16shl32_96 (.in_1(mul16shl32_89_out_2), .out_2(mul16shl32_96_out_2));
  mul16shl32 mul16shl32_97 (.in_1(mul16shl32_90_out_2), .out_2(mul16shl32_97_out_2));
  mul16shl32 mul16shl32_98 (.in_1(mul16shl32_91_out_2), .out_2(mul16shl32_98_out_2));
  mul16shl32 mul16shl32_99 (.in_1(mul16shl32_92_out_2), .out_2(mul16shl32_99_out_2));
  Adder #(.width(32)) adder_9 (
    .a(adder_8_out), .b(mul16shl32_93_out_2), .out(adder_9_out), .cin(adder_8_cout), .cout(adder_9_cout));
  mul16shl32 mul16shl32_100 (.in_1(mul16shl32_94_out_2), .out_2(mul16shl32_100_out_2));
  mul16shl32 mul16shl32_101 (.in_1(mul16shl32_95_out_2), .out_2(mul16shl32_101_out_2));
  mul16shl32 mul16shl32_102 (.in_1(mul16shl32_96_out_2), .out_2(mul16shl32_102_out_2));
  mul16shl32 mul16shl32_103 (.in_1(mul16shl32_97_out_2), .out_2(mul16shl32_103_out_2));
  mul16shl32 mul16shl32_104 (.in_1(mul16shl32_98_out_2), .out_2(mul16shl32_104_out_2));
  mul16shl32 mul16shl32_105 (.in_1(mul16shl32_99_out_2), .out_2(mul16shl32_105_out_2));
  Adder #(.width(32)) adder_10 (
    .a(adder_9_out), .b(mul16shl32_100_out_2), .out(adder_10_out), .cin(adder_9_cout), .cout(adder_10_cout));
  mul16shl32 mul16shl32_106 (.in_1(mul16shl32_101_out_2), .out_2(mul16shl32_106_out_2));
  mul16shl32 mul16shl32_107 (.in_1(mul16shl32_102_out_2), .out_2(mul16shl32_107_out_2));
  mul16shl32 mul16shl32_108 (.in_1(mul16shl32_103_out_2), .out_2(mul16shl32_108_out_2));
  mul16shl32 mul16shl32_109 (.in_1(mul16shl32_104_out_2), .out_2(mul16shl32_109_out_2));
  mul16shl32 mul16shl32_110 (.in_1(mul16shl32_105_out_2), .out_2(mul16shl32_110_out_2));
  Adder #(.width(32)) adder_11 (
    .a(adder_10_out), .b(mul16shl32_106_out_2), .out(adder_11_out), .cin(adder_10_cout), .cout(adder_11_cout));
  mul16shl32 mul16shl32_111 (.in_1(mul16shl32_107_out_2), .out_2(mul16shl32_111_out_2));
  mul16shl32 mul16shl32_112 (.in_1(mul16shl32_108_out_2), .out_2(mul16shl32_112_out_2));
  mul16shl32 mul16shl32_113 (.in_1(mul16shl32_109_out_2), .out_2(mul16shl32_113_out_2));
  mul16shl32 mul16shl32_114 (.in_1(mul16shl32_110_out_2), .out_2(mul16shl32_114_out_2));
  Adder #(.width(32)) adder_12 (
    .a(adder_11_out), .b(mul16shl32_111_out_2), .out(adder_12_out), .cin(adder_11_cout), .cout(adder_12_cout));
  mul16shl32 mul16shl32_115 (.in_1(mul16shl32_112_out_2), .out_2(mul16shl32_115_out_2));
  mul16shl32 mul16shl32_116 (.in_1(mul16shl32_113_out_2), .out_2(mul16shl32_116_out_2));
  mul16shl32 mul16shl32_117 (.in_1(mul16shl32_114_out_2), .out_2(mul16shl32_117_out_2));
  Adder #(.width(32)) adder_13 (
    .a(adder_12_out), .b(mul16shl32_115_out_2), .out(adder_13_out), .cin(adder_12_cout), .cout(adder_13_cout));
  mul16shl32 mul16shl32_118 (.in_1(mul16shl32_116_out_2), .out_2(mul16shl32_118_out_2));
  mul16shl32 mul16shl32_119 (.in_1(mul16shl32_117_out_2), .out_2(mul16shl32_119_out_2));
  Adder #(.width(32)) adder_14 (
    .a(adder_13_out), .b(mul16shl32_118_out_2), .out(adder_14_out), .cin(adder_13_cout), .cout(adder_14_cout));
  mul16shl32 mul16shl32_120 (.in_1(mul16shl32_119_out_2), .out_2(mul16shl32_120_out_2));
  Adder #(.width(32)) adder_15 (
    .a(adder_14_out), .b(mul16shl32_120_out_2), .out({Hout, Lout}), .cin(adder_14_cout));  // open: cout
endmodule

module mul16shl32 (
  input  [31:0] in_1,
  output [31:0] out_2
);


  assign out_2 = {in_1[30:0], in_1[31]};
endmodule

module mul32 (
  input  [31:0] A,
  input  [31:0] B,
  output [31:0] Lout,
  output [31:0] Hout
);

  wire adder_1_cout, adder_2_cout, adder_3_cout, adder_4_cout, adder_5_cout, adder_6_cout, adder_7_cout,
       adder_8_cout, adder_9_cout, adder_10_cout, adder_11_cout, adder_12_cout, adder_13_cout, adder_14_cout,
       adder_15_cout, adder_16_cout, adder_17_cout, adder_18_cout, adder_19_cout, adder_20_cout,
       adder_21_cout, adder_22_cout, adder_23_cout, adder_24_cout, adder_25_cout, adder_26_cout,
       adder_27_cout, adder_28_cout, adder_29_cout, adder_30_cout;
  wire [31:0] and_1_out, and_2_out, and_3_out, and_4_out, and_5_out, and_6_out, and_7_out, and_8_out,
       and_9_out, and_10_out, and_11_out, and_12_out, and_13_out, and_14_out, and_15_out, and_16_out,
       and_17_out, and_18_out, and_19_out, and_20_out, and_21_out, and_22_out, and_23_out, and_24_out,
       and_25_out, and_26_out, and_27_out, and_28_out, and_29_out, and_30_out, and_31_out, and_32_out,
       bit_extender_1_out, bit_extender_2_out, bit_extender_3_out, bit_extender_4_out, bit_extender_5_out,
       bit_extender_6_out, bit_extender_7_out, bit_extender_8_out, bit_extender_9_out, bit_extender_10_out,
       bit_extender_11_out, bit_extender_12_out, bit_extender_13_out, bit_extender_14_out,
       bit_extender_15_out, bit_extender_16_out, bit_extender_17_out, bit_extender_18_out,
       bit_extender_19_out, bit_extender_20_out, bit_extender_21_out, bit_extender_22_out,
       bit_extender_23_out, bit_extender_24_out, bit_extender_25_out, bit_extender_26_out,
       bit_extender_27_out, bit_extender_28_out, bit_extender_29_out, bit_extender_30_out,
       bit_extender_31_out, bit_extender_32_out;
  wire [63:0] adder_1_out, adder_2_out, adder_3_out, adder_4_out, adder_5_out, adder_6_out, adder_7_out,
       adder_8_out, adder_9_out, adder_10_out, adder_11_out, adder_12_out, adder_13_out, adder_14_out,
       adder_15_out, adder_16_out, adder_17_out, adder_18_out, adder_19_out, adder_20_out, adder_21_out,
       adder_22_out, adder_23_out, adder_24_out, adder_25_out, adder_26_out, adder_27_out, adder_28_out,
       adder_29_out, adder_30_out, bit_extender_33_out, bit_extender_34_out, bit_extender_35_out,
       bit_extender_36_out, bit_extender_37_out, bit_extender_38_out, bit_extender_39_out,
       bit_extender_40_out, bit_extender_41_out, bit_extender_42_out, bit_extender_43_out,
       bit_extender_44_out, bit_extender_45_out, bit_extender_46_out, bit_extender_47_out,
       bit_extender_48_out, bit_extender_49_out, bit_extender_50_out, bit_extender_51_out,
       bit_extender_52_out, bit_extender_53_out, bit_extender_54_out, bit_extender_55_out,
       bit_extender_56_out, bit_extender_57_out, bit_extender_58_out, bit_extender_59_out,
       bit_extender_60_out, bit_extender_61_out, bit_extender_62_out, bit_extender_63_out,
       bit_extender_64_out, rotl64_1_out_2, rotl64_2_out_2, rotl64_3_out_2, rotl64_4_out_2, rotl64_5_out_2,
       rotl64_6_out_2, rotl64_7_out_2, rotl64_8_out_2, rotl64_9_out_2, rotl64_10_out_2, rotl64_11_out_2,
       rotl64_12_out_2, rotl64_13_out_2, rotl64_14_out_2, rotl64_15_out_2, rotl64_16_out_2, rotl64_17_out_2,
       rotl64_18_out_2, rotl64_19_out_2, rotl64_20_out_2, rotl64_21_out_2, rotl64_22_out_2, rotl64_23_out_2,
       rotl64_24_out_2, rotl64_25_out_2, rotl64_26_out_2, rotl64_27_out_2, rotl64_28_out_2, rotl64_29_out_2,
       rotl64_30_out_2, rotl64_31_out_2, rotl64_32_out_2, rotl64_33_out_2, rotl64_34_out_2, rotl64_35_out_2,
       rotl64_36_out_2, rotl64_37_out_2, rotl64_38_out_2, rotl64_39_out_2, rotl64_40_out_2, rotl64_41_out_2,
       rotl64_42_out_2, rotl64_43_out_2, rotl64_44_out_2, rotl64_45_out_2, rotl64_46_out_2, rotl64_47_out_2,
       rotl64_48_out_2, rotl64_49_out_2, rotl64_50_out_2, rotl64_51_out_2, rotl64_52_out_2, rotl64_53_out_2,
       rotl64_54_out_2, rotl64_55_out_2, rotl64_56_out_2, rotl64_57_out_2, rotl64_58_out_2, rotl64_59_out_2,
       rotl64_60_out_2, rotl64_61_out_2, rotl64_62_out_2, rotl64_63_out_2, rotl64_64_out_2, rotl64_65_out_2,
       rotl64_66_out_2, rotl64_67_out_2, rotl64_68_out_2, rotl64_69_out_2, rotl64_70_out_2, rotl64_71_out_2,
       rotl64_72_out_2, rotl64_73_out_2, rotl64_74_out_2, rotl64_75_out_2, rotl64_76_out_2, rotl64_77_out_2,
       rotl64_78_out_2, rotl64_79_out_2, rotl64_80_out_2, rotl64_81_out_2, rotl64_82_out_2, rotl64_83_out_2,
       rotl64_84_out_2, rotl64_85_out_2, rotl64_86_out_2, rotl64_87_out_2, rotl64_88_out_2, rotl64_89_out_2,
       rotl64_90_out_2, rotl64_91_out_2, rotl64_92_out_2, rotl64_93_out_2, rotl64_94_out_2, rotl64_95_out_2,
       rotl64_96_out_2, rotl64_97_out_2, rotl64_98_out_2, rotl64_99_out_2, rotl64_100_out_2,
       rotl64_101_out_2, rotl64_102_out_2, rotl64_103_out_2, rotl64_104_out_2, rotl64_105_out_2,
       rotl64_106_out_2, rotl64_107_out_2, rotl64_108_out_2, rotl64_109_out_2, rotl64_110_out_2,
       rotl64_111_out_2, rotl64_112_out_2, rotl64_113_out_2, rotl64_114_out_2, rotl64_115_out_2,
       rotl64_116_out_2, rotl64_117_out_2, rotl64_118_out_2, rotl64_119_out_2, rotl64_120_out_2,
       rotl64_121_out_2, rotl64_122_out_2, rotl64_123_out_2, rotl64_124_out_2, rotl64_125_out_2,
       rotl64_126_out_2, rotl64_127_out_2, rotl64_128_out_2, rotl64_129_out_2, rotl64_130_out_2,
       rotl64_131_out_2, rotl64_132_out_2, rotl64_133_out_2, rotl64_134_out_2, rotl64_135_out_2,
       rotl64_136_out_2, rotl64_137_out_2, rotl64_138_out_2, rotl64_139_out_2, rotl64_140_out_2,
       rotl64_141_out_2, rotl64_142_out_2, rotl64_143_out_2, rotl64_144_out_2, rotl64_145_out_2,
       rotl64_146_out_2, rotl64_147_out_2, rotl64_148_out_2, rotl64_149_out_2, rotl64_150_out_2,
       rotl64_151_out_2, rotl64_152_out_2, rotl64_153_out_2, rotl64_154_out_2, rotl64_155_out_2,
       rotl64_156_out_2, rotl64_157_out_2, rotl64_158_out_2, rotl64_159_out_2, rotl64_160_out_2,
       rotl64_161_out_2, rotl64_162_out_2, rotl64_163_out_2, rotl64_164_out_2, rotl64_165_out_2,
       rotl64_166_out_2, rotl64_167_out_2, rotl64_168_out_2, rotl64_169_out_2, rotl64_170_out_2,
       rotl64_171_out_2, rotl64_172_out_2, rotl64_173_out_2, rotl64_174_out_2, rotl64_175_out_2,
       rotl64_176_out_2, rotl64_177_out_2, rotl64_178_out_2, rotl64_179_out_2, rotl64_180_out_2,
       rotl64_181_out_2, rotl64_182_out_2, rotl64_183_out_2, rotl64_184_out_2, rotl64_185_out_2,
       rotl64_186_out_2, rotl64_187_out_2, rotl64_188_out_2, rotl64_189_out_2, rotl64_190_out_2,
       rotl64_191_out_2, rotl64_192_out_2, rotl64_193_out_2, rotl64_194_out_2, rotl64_195_out_2,
       rotl64_196_out_2, rotl64_197_out_2, rotl64_198_out_2, rotl64_199_out_2, rotl64_200_out_2,
       rotl64_201_out_2, rotl64_202_out_2, rotl64_203_out_2, rotl64_204_out_2, rotl64_205_out_2,
       rotl64_206_out_2, rotl64_207_out_2, rotl64_208_out_2, rotl64_209_out_2, rotl64_210_out_2,
       rotl64_211_out_2, rotl64_212_out_2, rotl64_213_out_2, rotl64_214_out_2, rotl64_215_out_2,
       rotl64_216_out_2, rotl64_217_out_2, rotl64_218_out_2, rotl64_219_out_2, rotl64_220_out_2,
       rotl64_221_out_2, rotl64_222_out_2, rotl64_223_out_2, rotl64_224_out_2, rotl64_225_out_2,
       rotl64_226_out_2, rotl64_227_out_2, rotl64_228_out_2, rotl64_229_out_2, rotl64_230_out_2,
       rotl64_231_out_2, rotl64_232_out_2, rotl64_233_out_2, rotl64_234_out_2, rotl64_235_out_2,
       rotl64_236_out_2, rotl64_237_out_2, rotl64_238_out_2, rotl64_239_out_2, rotl64_240_out_2,
       rotl64_241_out_2, rotl64_242_out_2, rotl64_243_out_2, rotl64_244_out_2, rotl64_245_out_2,
       rotl64_246_out_2, rotl64_247_out_2, rotl64_248_out_2, rotl64_249_out_2, rotl64_250_out_2,
       rotl64_251_out_2, rotl64_252_out_2, rotl64_253_out_2, rotl64_254_out_2, rotl64_255_out_2,
       rotl64_256_out_2, rotl64p16_1_out_2, rotl64p16_2_out_2, rotl64p16_3_out_2, rotl64p16_4_out_2,
       rotl64p16_5_out_2, rotl64p16_6_out_2, rotl64p16_7_out_2, rotl64p16_8_out_2, rotl64p16_9_out_2,
       rotl64p16_10_out_2, rotl64p16_11_out_2, rotl64p16_12_out_2, rotl64p16_13_out_2, rotl64p16_14_out_2,
       rotl64p16_15_out_2, rotl64p16_16_out_2;

  assign bit_extender_1_out = {{31{A[0]}}, A[0]};  // Bit_Extender bit_extender_1
  assign bit_extender_2_out = {{31{A[1]}}, A[1]};  // Bit_Extender bit_extender_2
  assign bit_extender_3_out = {{31{A[2]}}, A[2]};  // Bit_Extender bit_extender_3
  assign bit_extender_4_out = {{31{A[3]}}, A[3]};  // Bit_Extender bit_extender_4
  assign bit_extender_5_out = {{31{A[4]}}, A[4]};  // Bit_Extender bit_extender_5
  assign bit_extender_6_out = {{31{A[5]}}, A[5]};  // Bit_Extender bit_extender_6
  assign bit_extender_7_out = {{31{A[6]}}, A[6]};  // Bit_Extender bit_extender_7
  assign bit_extender_8_out = {{31{A[7]}}, A[7]};  // Bit_Extender bit_extender_8
  assign bit_extender_9_out = {{31{A[8]}}, A[8]};  // Bit_Extender bit_extender_9
  assign bit_extender_10_out = {{31{A[9]}}, A[9]};  // Bit_Extender bit_extender_10
  assign bit_extender_11_out = {{31{A[10]}}, A[10]};  // Bit_Extender bit_extender_11
  assign bit_extender_12_out = {{31{A[11]}}, A[11]};  // Bit_Extender bit_extender_12
  assign bit_extender_13_out = {{31{A[12]}}, A[12]};  // Bit_Extender bit_extender_13
  assign bit_extender_14_out = {{31{A[13]}}, A[13]};  // Bit_Extender bit_extender_14
  assign bit_extender_15_out = {{31{A[14]}}, A[14]};  // Bit_Extender bit_extender_15
  assign bit_extender_16_out = {{31{A[15]}}, A[15]};  // Bit_Extender bit_extender_16
  assign bit_extender_17_out = {{31{A[16]}}, A[16]};  // Bit_Extender bit_extender_17
  assign bit_extender_18_out = {{31{A[17]}}, A[17]};  // Bit_Extender bit_extender_18
  assign bit_extender_19_out = {{31{A[18]}}, A[18]};  // Bit_Extender bit_extender_19
  assign bit_extender_20_out = {{31{A[19]}}, A[19]};  // Bit_Extender bit_extender_20
  assign bit_extender_21_out = {{31{A[20]}}, A[20]};  // Bit_Extender bit_extender_21
  assign bit_extender_22_out = {{31{A[21]}}, A[21]};  // Bit_Extender bit_extender_22
  assign bit_extender_23_out = {{31{A[22]}}, A[22]};  // Bit_Extender bit_extender_23
  assign bit_extender_24_out = {{31{A[23]}}, A[23]};  // Bit_Extender bit_extender_24
  assign bit_extender_25_out = {{31{A[24]}}, A[24]};  // Bit_Extender bit_extender_25
  assign bit_extender_26_out = {{31{A[25]}}, A[25]};  // Bit_Extender bit_extender_26
  assign bit_extender_27_out = {{31{A[26]}}, A[26]};  // Bit_Extender bit_extender_27
  assign bit_extender_28_out = {{31{A[27]}}, A[27]};  // Bit_Extender bit_extender_28
  assign bit_extender_29_out = {{31{A[28]}}, A[28]};  // Bit_Extender bit_extender_29
  assign bit_extender_30_out = {{31{A[29]}}, A[29]};  // Bit_Extender bit_extender_30
  assign bit_extender_31_out = {{31{A[30]}}, A[30]};  // Bit_Extender bit_extender_31
  assign bit_extender_32_out = {{31{A[31]}}, A[31]};  // Bit_Extender bit_extender_32
  assign and_1_out = B & bit_extender_1_out;  // AND_Gate and_1, 32 bits wide
  assign and_2_out = B & bit_extender_2_out;  // AND_Gate and_2, 32 bits wide
  assign and_3_out = B & bit_extender_3_out;  // AND_Gate and_3, 32 bits wide
  assign and_4_out = B & bit_extender_4_out;  // AND_Gate and_4, 32 bits wide
  assign and_5_out = B & bit_extender_5_out;  // AND_Gate and_5, 32 bits wide
  assign and_6_out = B & bit_extender_6_out;  // AND_Gate and_6, 32 bits wide
  assign and_7_out = B & bit_extender_7_out;  // AND_Gate and_7, 32 bits wide
  assign and_8_out = B & bit_extender_8_out;  // AND_Gate and_8, 32 bits wide
  assign and_9_out = B & bit_extender_9_out;  // AND_Gate and_9, 32 bits wide
  assign and_10_out = B & bit_extender_10_out;  // AND_Gate and_10, 32 bits wide
  assign and_11_out = B & bit_extender_11_out;  // AND_Gate and_11, 32 bits wide
  assign and_12_out = B & bit_extender_12_out;  // AND_Gate and_12, 32 bits wide
  assign and_13_out = B & bit_extender_13_out;  // AND_Gate and_13, 32 bits wide
  assign and_14_out = B & bit_extender_14_out;  // AND_Gate and_14, 32 bits wide
  assign and_15_out = B & bit_extender_15_out;  // AND_Gate and_15, 32 bits wide
  assign and_16_out = B & bit_extender_16_out;  // AND_Gate and_16, 32 bits wide
  assign and_17_out = B & bit_extender_17_out;  // AND_Gate and_17, 32 bits wide
  assign and_18_out = B & bit_extender_18_out;  // AND_Gate and_18, 32 bits wide
  assign and_19_out = B & bit_extender_19_out;  // AND_Gate and_19, 32 bits wide
  assign and_20_out = B & bit_extender_20_out;  // AND_Gate and_20, 32 bits wide
  assign and_21_out = B & bit_extender_21_out;  // AND_Gate and_21, 32 bits wide
  assign and_22_out = B & bit_extender_22_out;  // AND_Gate and_22, 32 bits wide
  assign and_23_out = B & bit_extender_23_out;  // AND_Gate and_23, 32 bits wide
  assign and_24_out = B & bit_extender_24_out;  // AND_Gate and_24, 32 bits wide
  assign and_25_out = B & bit_extender_25_out;  // AND_Gate and_25, 32 bits wide
  assign and_26_out = B & bit_extender_26_out;  // AND_Gate and_26, 32 bits wide
  assign and_27_out = B & bit_extender_27_out;  // AND_Gate and_27, 32 bits wide
  assign and_28_out = B & bit_extender_28_out;  // AND_Gate and_28, 32 bits wide
  assign and_29_out = B & bit_extender_29_out;  // AND_Gate and_29, 32 bits wide
  assign and_30_out = B & bit_extender_30_out;  // AND_Gate and_30, 32 bits wide
  assign and_31_out = B & bit_extender_31_out;  // AND_Gate and_31, 32 bits wide
  assign and_32_out = B & bit_extender_32_out;  // AND_Gate and_32, 32 bits wide
  assign bit_extender_33_out = {{32{1'b0}}, and_1_out};  // Bit_Extender bit_extender_33
  assign bit_extender_34_out = {{32{1'b0}}, and_2_out};  // Bit_Extender bit_extender_34
  assign bit_extender_35_out = {{32{1'b0}}, and_3_out};  // Bit_Extender bit_extender_35
  assign bit_extender_36_out = {{32{1'b0}}, and_4_out};  // Bit_Extender bit_extender_36
  assign bit_extender_37_out = {{32{1'b0}}, and_5_out};  // Bit_Extender bit_extender_37
  assign bit_extender_38_out = {{32{1'b0}}, and_6_out};  // Bit_Extender bit_extender_38
  assign bit_extender_39_out = {{32{1'b0}}, and_7_out};  // Bit_Extender bit_extender_39
  assign bit_extender_40_out = {{32{1'b0}}, and_8_out};  // Bit_Extender bit_extender_40
  assign bit_extender_41_out = {{32{1'b0}}, and_9_out};  // Bit_Extender bit_extender_41
  assign bit_extender_42_out = {{32{1'b0}}, and_10_out};  // Bit_Extender bit_extender_42
  assign bit_extender_43_out = {{32{1'b0}}, and_11_out};  // Bit_Extender bit_extender_43
  assign bit_extender_44_out = {{32{1'b0}}, and_12_out};  // Bit_Extender bit_extender_44
  assign bit_extender_45_out = {{32{1'b0}}, and_13_out};  // Bit_Extender bit_extender_45
  assign bit_extender_46_out = {{32{1'b0}}, and_14_out};  // Bit_Extender bit_extender_46
  assign bit_extender_47_out = {{32{1'b0}}, and_15_out};  // Bit_Extender bit_extender_47
  assign bit_extender_48_out = {{32{1'b0}}, and_16_out};  // Bit_Extender bit_extender_48
  assign bit_extender_49_out = {{32{1'b0}}, and_17_out};  // Bit_Extender bit_extender_49
  assign bit_extender_50_out = {{32{1'b0}}, and_18_out};  // Bit_Extender bit_extender_50
  assign bit_extender_51_out = {{32{1'b0}}, and_19_out};  // Bit_Extender bit_extender_51
  assign bit_extender_52_out = {{32{1'b0}}, and_20_out};  // Bit_Extender bit_extender_52
  assign bit_extender_53_out = {{32{1'b0}}, and_21_out};  // Bit_Extender bit_extender_53
  assign bit_extender_54_out = {{32{1'b0}}, and_22_out};  // Bit_Extender bit_extender_54
  assign bit_extender_55_out = {{32{1'b0}}, and_23_out};  // Bit_Extender bit_extender_55
  assign bit_extender_56_out = {{32{1'b0}}, and_24_out};  // Bit_Extender bit_extender_56
  assign bit_extender_57_out = {{32{1'b0}}, and_25_out};  // Bit_Extender bit_extender_57
  assign bit_extender_58_out = {{32{1'b0}}, and_26_out};  // Bit_Extender bit_extender_58
  assign bit_extender_59_out = {{32{1'b0}}, and_27_out};  // Bit_Extender bit_extender_59
  assign bit_extender_60_out = {{32{1'b0}}, and_28_out};  // Bit_Extender bit_extender_60
  assign bit_extender_61_out = {{32{1'b0}}, and_29_out};  // Bit_Extender bit_extender_61
  assign bit_extender_62_out = {{32{1'b0}}, and_30_out};  // Bit_Extender bit_extender_62
  assign bit_extender_63_out = {{32{1'b0}}, and_31_out};  // Bit_Extender bit_extender_63
  assign bit_extender_64_out = {{32{1'b0}}, and_32_out};  // Bit_Extender bit_extender_64
  rotl64 rotl64_1 (.in_1(bit_extender_34_out), .out_2(rotl64_1_out_2));
  rotl64 rotl64_2 (.in_1(bit_extender_35_out), .out_2(rotl64_2_out_2));
  rotl64 rotl64_3 (.in_1(bit_extender_36_out), .out_2(rotl64_3_out_2));
  rotl64 rotl64_4 (.in_1(bit_extender_37_out), .out_2(rotl64_4_out_2));
  rotl64 rotl64_5 (.in_1(bit_extender_38_out), .out_2(rotl64_5_out_2));
  rotl64 rotl64_6 (.in_1(bit_extender_39_out), .out_2(rotl64_6_out_2));
  rotl64 rotl64_7 (.in_1(bit_extender_40_out), .out_2(rotl64_7_out_2));
  rotl64 rotl64_8 (.in_1(bit_extender_41_out), .out_2(rotl64_8_out_2));
  rotl64 rotl64_9 (.in_1(bit_extender_42_out), .out_2(rotl64_9_out_2));
  rotl64 rotl64_10 (.in_1(bit_extender_43_out), .out_2(rotl64_10_out_2));
  rotl64 rotl64_11 (.in_1(bit_extender_44_out), .out_2(rotl64_11_out_2));
  rotl64 rotl64_12 (.in_1(bit_extender_45_out), .out_2(rotl64_12_out_2));
  rotl64 rotl64_13 (.in_1(bit_extender_46_out), .out_2(rotl64_13_out_2));
  rotl64 rotl64_14 (.in_1(bit_extender_47_out), .out_2(rotl64_14_out_2));
  rotl64 rotl64_15 (.in_1(bit_extender_48_out), .out_2(rotl64_15_out_2));
  rotl64p16 rotl64p16_1 (.in_1(bit_extender_49_out), .out_2(rotl64p16_1_out_2));
  rotl64p16 rotl64p16_2 (.in_1(bit_extender_50_out), .out_2(rotl64p16_2_out_2));
  rotl64p16 rotl64p16_3 (.in_1(bit_extender_51_out), .out_2(rotl64p16_3_out_2));
  rotl64p16 rotl64p16_4 (.in_1(bit_extender_52_out), .out_2(rotl64p16_4_out_2));
  rotl64p16 rotl64p16_5 (.in_1(bit_extender_53_out), .out_2(rotl64p16_5_out_2));
  rotl64p16 rotl64p16_6 (.in_1(bit_extender_54_out), .out_2(rotl64p16_6_out_2));
  rotl64p16 rotl64p16_7 (.in_1(bit_extender_55_out), .out_2(rotl64p16_7_out_2));
  rotl64p16 rotl64p16_8 (.in_1(bit_extender_56_out), .out_2(rotl64p16_8_out_2));
  rotl64p16 rotl64p16_9 (.in_1(bit_extender_57_out), .out_2(rotl64p16_9_out_2));
  rotl64p16 rotl64p16_10 (.in_1(bit_extender_58_out), .out_2(rotl64p16_10_out_2));
  rotl64p16 rotl64p16_11 (.in_1(bit_extender_59_out), .out_2(rotl64p16_11_out_2));
  rotl64p16 rotl64p16_12 (.in_1(bit_extender_60_out), .out_2(rotl64p16_12_out_2));
  rotl64p16 rotl64p16_13 (.in_1(bit_extender_61_out), .out_2(rotl64p16_13_out_2));
  rotl64p16 rotl64p16_14 (.in_1(bit_extender_62_out), .out_2(rotl64p16_14_out_2));
  rotl64p16 rotl64p16_15 (.in_1(bit_extender_63_out), .out_2(rotl64p16_15_out_2));
  rotl64p16 rotl64p16_16 (.in_1(bit_extender_64_out), .out_2(rotl64p16_16_out_2));
  Adder #(.width(64)) adder_1 (
    .a(bit_extender_33_out), .b(rotl64_1_out_2), .out(adder_1_out), .cin(1'b0), .cout(adder_1_cout));
  rotl64 rotl64_16 (.in_1(rotl64_2_out_2), .out_2(rotl64_16_out_2));
  rotl64 rotl64_17 (.in_1(rotl64_3_out_2), .out_2(rotl64_17_out_2));
  rotl64 rotl64_18 (.in_1(rotl64_4_out_2), .out_2(rotl64_18_out_2));
  rotl64 rotl64_19 (.in_1(rotl64_5_out_2), .out_2(rotl64_19_out_2));
  rotl64 rotl64_20 (.in_1(rotl64_6_out_2), .out_2(rotl64_20_out_2));
  rotl64 rotl64_21 (.in_1(rotl64_7_out_2), .out_2(rotl64_21_out_2));
  rotl64 rotl64_22 (.in_1(rotl64_8_out_2), .out_2(rotl64_22_out_2));
  rotl64 rotl64_23 (.in_1(rotl64_9_out_2), .out_2(rotl64_23_out_2));
  rotl64 rotl64_24 (.in_1(rotl64_10_out_2), .out_2(rotl64_24_out_2));
  rotl64 rotl64_25 (.in_1(rotl64_11_out_2), .out_2(rotl64_25_out_2));
  rotl64 rotl64_26 (.in_1(rotl64_12_out_2), .out_2(rotl64_26_out_2));
  rotl64 rotl64_27 (.in_1(rotl64_13_out_2), .out_2(rotl64_27_out_2));
  rotl64 rotl64_28 (.in_1(rotl64_14_out_2), .out_2(rotl64_28_out_2));
  rotl64 rotl64_29 (.in_1(rotl64_15_out_2), .out_2(rotl64_29_out_2));
  rotl64 rotl64_30 (.in_1(rotl64p16_1_out_2), .out_2(rotl64_30_out_2));
  rotl64 rotl64_31 (.in_1(rotl64p16_2_out_2), .out_2(rotl64_31_out_2));
  rotl64 rotl64_32 (.in_1(rotl64p16_3_out_2), .out_2(rotl64_32_out_2));
  rotl64 rotl64_33 (.in_1(rotl64p16_4_out_2), .out_2(rotl64_33_out_2));
  rotl64 rotl64_34 (.in_1(rotl64p16_5_out_2), .out_2(rotl64_34_out_2));
  rotl64 rotl64_35 (.in_1(rotl64p16_6_out_2), .out_2(rotl64_35_out_2));
  rotl64 rotl64_36 (.in_1(rotl64p16_7_out_2), .out_2(rotl64_36_out_2));
  rotl64 rotl64_37 (.in_1(rotl64p16_8_out_2), .out_2(rotl64_37_out_2));
  rotl64 rotl64_38 (.in_1(rotl64p16_9_out_2), .out_2(rotl64_38_out_2));
  rotl64 rotl64_39 (.in_1(rotl64p16_10_out_2), .out_2(rotl64_39_out_2));
  rotl64 rotl64_40 (.in_1(rotl64p16_11_out_2), .out_2(rotl64_40_out_2));
  rotl64 rotl64_41 (.in_1(rotl64p16_12_out_2), .out_2(rotl64_41_out_2));
  rotl64 rotl64_42 (.in_1(rotl64p16_13_out_2), .out_2(rotl64_42_out_2));
  rotl64 rotl64_43 (.in_1(rotl64p16_14_out_2), .out_2(rotl64_43_out_2));
  rotl64 rotl64_44 (.in_1(rotl64p16_15_out_2), .out_2(rotl64_44_out_2));
  rotl64 rotl64_45 (.in_1(rotl64p16_16_out_2), .out_2(rotl64_45_out_2));
  Adder #(.width(64)) adder_2 (
    .a(adder_1_out), .b(rotl64_16_out_2), .out(adder_2_out), .cin(adder_1_cout), .cout(adder_2_cout));
  rotl64 rotl64_46 (.in_1(rotl64_17_out_2), .out_2(rotl64_46_out_2));
  rotl64 rotl64_47 (.in_1(rotl64_18_out_2), .out_2(rotl64_47_out_2));
  rotl64 rotl64_48 (.in_1(rotl64_19_out_2), .out_2(rotl64_48_out_2));
  rotl64 rotl64_49 (.in_1(rotl64_20_out_2), .out_2(rotl64_49_out_2));
  rotl64 rotl64_50 (.in_1(rotl64_21_out_2), .out_2(rotl64_50_out_2));
  rotl64 rotl64_51 (.in_1(rotl64_22_out_2), .out_2(rotl64_51_out_2));
  rotl64 rotl64_52 (.in_1(rotl64_23_out_2), .out_2(rotl64_52_out_2));
  rotl64 rotl64_53 (.in_1(rotl64_24_out_2), .out_2(rotl64_53_out_2));
  rotl64 rotl64_54 (.in_1(rotl64_25_out_2), .out_2(rotl64_54_out_2));
  rotl64 rotl64_55 (.in_1(rotl64_26_out_2), .out_2(rotl64_55_out_2));
  rotl64 rotl64_56 (.in_1(rotl64_27_out_2), .out_2(rotl64_56_out_2));
  rotl64 rotl64_57 (.in_1(rotl64_28_out_2), .out_2(rotl64_57_out_2));
  rotl64 rotl64_58 (.in_1(rotl64_29_out_2), .out_2(rotl64_58_out_2));
  Adder #(.width(64)) adder_3 (
    .a(rotl64_30_out_2), .b(adder_28_out), .out(adder_3_out), .cin(adder_28_cout), .cout(adder_3_cout));
  rotl64 rotl64_59 (.in_1(rotl64_31_out_2), .out_2(rotl64_59_out_2));
  rotl64 rotl64_60 (.in_1(rotl64_32_out_2), .out_2(rotl64_60_out_2));
  rotl64 rotl64_61 (.in_1(rotl64_33_out_2), .out_2(rotl64_61_out_2));
  rotl64 rotl64_62 (.in_1(rotl64_34_out_2), .out_2(rotl64_62_out_2));
  rotl64 rotl64_63 (.in_1(rotl64_35_out_2), .out_2(rotl64_63_out_2));
  rotl64 rotl64_64 (.in_1(rotl64_36_out_2), .out_2(rotl64_64_out_2));
  rotl64 rotl64_65 (.in_1(rotl64_37_out_2), .out_2(rotl64_65_out_2));
  rotl64 rotl64_66 (.in_1(rotl64_38_out_2), .out_2(rotl64_66_out_2));
  rotl64 rotl64_67 (.in_1(rotl64_39_out_2), .out_2(rotl64_67_out_2));
  rotl64 rotl64_68 (.in_1(rotl64_40_out_2), .out_2(rotl64_68_out_2));
  rotl64 rotl64_69 (.in_1(rotl64_41_out_2), .out_2(rotl64_69_out_2));
  rotl64 rotl64_70 (.in_1(rotl64_42_out_2), .out_2(rotl64_70_out_2));
  rotl64 rotl64_71 (.in_1(rotl64_43_out_2), .out_2(rotl64_71_out_2));
  rotl64 rotl64_72 (.in_1(rotl64_44_out_2), .out_2(rotl64_72_out_2));
  rotl64 rotl64_73 (.in_1(rotl64_45_out_2), .out_2(rotl64_73_out_2));
  Adder #(.width(64)) adder_4 (
    .a(adder_2_out), .b(rotl64_46_out_2), .out(adder_4_out), .cin(adder_2_cout), .cout(adder_4_cout));
  Adder #(.width(64)) adder_5 (
    .a(adder_3_out), .b(rotl64_59_out_2), .out(adder_5_out), .cin(adder_3_cout), .cout(adder_5_cout));
  rotl64 rotl64_74 (.in_1(rotl64_47_out_2), .out_2(rotl64_74_out_2));
  rotl64 rotl64_75 (.in_1(rotl64_48_out_2), .out_2(rotl64_75_out_2));
  rotl64 rotl64_76 (.in_1(rotl64_49_out_2), .out_2(rotl64_76_out_2));
  rotl64 rotl64_77 (.in_1(rotl64_50_out_2), .out_2(rotl64_77_out_2));
  rotl64 rotl64_78 (.in_1(rotl64_51_out_2), .out_2(rotl64_78_out_2));
  rotl64 rotl64_79 (.in_1(rotl64_52_out_2), .out_2(rotl64_79_out_2));
  rotl64 rotl64_80 (.in_1(rotl64_53_out_2), .out_2(rotl64_80_out_2));
  rotl64 rotl64_81 (.in_1(rotl64_54_out_2), .out_2(rotl64_81_out_2));
  rotl64 rotl64_82 (.in_1(rotl64_55_out_2), .out_2(rotl64_82_out_2));
  rotl64 rotl64_83 (.in_1(rotl64_56_out_2), .out_2(rotl64_83_out_2));
  rotl64 rotl64_84 (.in_1(rotl64_57_out_2), .out_2(rotl64_84_out_2));
  rotl64 rotl64_85 (.in_1(rotl64_58_out_2), .out_2(rotl64_85_out_2));
  rotl64 rotl64_86 (.in_1(rotl64_60_out_2), .out_2(rotl64_86_out_2));
  rotl64 rotl64_87 (.in_1(rotl64_61_out_2), .out_2(rotl64_87_out_2));
  rotl64 rotl64_88 (.in_1(rotl64_62_out_2), .out_2(rotl64_88_out_2));
  rotl64 rotl64_89 (.in_1(rotl64_63_out_2), .out_2(rotl64_89_out_2));
  rotl64 rotl64_90 (.in_1(rotl64_64_out_2), .out_2(rotl64_90_out_2));
  rotl64 rotl64_91 (.in_1(rotl64_65_out_2), .out_2(rotl64_91_out_2));
  rotl64 rotl64_92 (.in_1(rotl64_66_out_2), .out_2(rotl64_92_out_2));
  rotl64 rotl64_93 (.in_1(rotl64_67_out_2), .out_2(rotl64_93_out_2));
  rotl64 rotl64_94 (.in_1(rotl64_68_out_2), .out_2(rotl64_94_out_2));
  rotl64 rotl64_95 (.in_1(rotl64_69_out_2), .out_2(rotl64_95_out_2));
  rotl64 rotl64_96 (.in_1(rotl64_70_out_2), .out_2(rotl64_96_out_2));
  rotl64 rotl64_97 (.in_1(rotl64_71_out_2), .out_2(rotl64_97_out_2));
  rotl64 rotl64_98 (.in_1(rotl64_72_out_2), .out_2(rotl64_98_out_2));
  rotl64 rotl64_99 (.in_1(rotl64_73_out_2), .out_2(rotl64_99_out_2));
  Adder #(.width(64)) adder_6 (
    .a(adder_4_out), .b(rotl64_74_out_2), .out(adder_6_out), .cin(adder_4_cout), .cout(adder_6_cout));
  Adder #(.width(64)) adder_7 (
    .a(adder_5_out), .b(rotl64_86_out_2), .out(adder_7_out), .cin(adder_5_cout), .cout(adder_7_cout));
  rotl64 rotl64_100 (.in_1(rotl64_75_out_2), .out_2(rotl64_100_out_2));
  rotl64 rotl64_101 (.in_1(rotl64_76_out_2), .out_2(rotl64_101_out_2));
  rotl64 rotl64_102 (.in_1(rotl64_77_out_2), .out_2(rotl64_102_out_2));
  rotl64 rotl64_103 (.in_1(rotl64_78_out_2), .out_2(rotl64_103_out_2));
  rotl64 rotl64_104 (.in_1(rotl64_79_out_2), .out_2(rotl64_104_out_2));
  rotl64 rotl64_105 (.in_1(rotl64_80_out_2), .out_2(rotl64_105_out_2));
  rotl64 rotl64_106 (.in_1(rotl64_81_out_2), .out_2(rotl64_106_out_2));
  rotl64 rotl64_107 (.in_1(rotl64_82_out_2), .out_2(rotl64_107_out_2));
  rotl64 rotl64_108 (.in_1(rotl64_83_out_2), .out_2(rotl64_108_out_2));
  rotl64 rotl64_109 (.in_1(rotl64_84_out_2), .out_2(rotl64_109_out_2));
  rotl64 rotl64_110 (.in_1(rotl64_85_out_2), .out_2(rotl64_110_out_2));
  rotl64 rotl64_111 (.in_1(rotl64_87_out_2), .out_2(rotl64_111_out_2));
  rotl64 rotl64_112 (.in_1(rotl64_88_out_2), .out_2(rotl64_112_out_2));
  rotl64 rotl64_113 (.in_1(rotl64_89_out_2), .out_2(rotl64_113_out_2));
  rotl64 rotl64_114 (.in_1(rotl64_90_out_2), .out_2(rotl64_114_out_2));
  rotl64 rotl64_115 (.in_1(rotl64_91_out_2), .out_2(rotl64_115_out_2));
  rotl64 rotl64_116 (.in_1(rotl64_92_out_2), .out_2(rotl64_116_out_2));
  rotl64 rotl64_117 (.in_1(rotl64_93_out_2), .out_2(rotl64_117_out_2));
  rotl64 rotl64_118 (.in_1(rotl64_94_out_2), .out_2(rotl64_118_out_2));
  rotl64 rotl64_119 (.in_1(rotl64_95_out_2), .out_2(rotl64_119_out_2));
  rotl64 rotl64_120 (.in_1(rotl64_96_out_2), .out_2(rotl64_120_out_2));
  rotl64 rotl64_121 (.in_1(rotl64_97_out_2), .out_2(rotl64_121_out_2));
  rotl64 rotl64_122 (.in_1(rotl64_98_out_2), .out_2(rotl64_122_out_2));
  rotl64 rotl64_123 (.in_1(rotl64_99_out_2), .out_2(rotl64_123_out_2));
  Adder #(.width(64)) adder_8 (
    .a(adder_6_out), .b(rotl64_100_out_2), .out(adder_8_out), .cin(adder_6_cout), .cout(adder_8_cout));
  Adder #(.width(64)) adder_9 (
    .a(adder_7_out), .b(rotl64_111_out_2), .out(adder_9_out), .cin(adder_7_cout), .cout(adder_9_cout));
  rotl64 rotl64_124 (.in_1(rotl64_101_out_2), .out_2(rotl64_124_out_2));
  rotl64 rotl64_125 (.in_1(rotl64_102_out_2), .out_2(rotl64_125_out_2));
  rotl64 rotl64_126 (.in_1(rotl64_103_out_2), .out_2(rotl64_126_out_2));
  rotl64 rotl64_127 (.in_1(rotl64_104_out_2), .out_2(rotl64_127_out_2));
  rotl64 rotl64_128 (.in_1(rotl64_105_out_2), .out_2(rotl64_128_out_2));
  rotl64 rotl64_129 (.in_1(rotl64_106_out_2), .out_2(rotl64_129_out_2));
  rotl64 rotl64_130 (.in_1(rotl64_107_out_2), .out_2(rotl64_130_out_2));
  rotl64 rotl64_131 (.in_1(rotl64_108_out_2), .out_2(rotl64_131_out_2));
  rotl64 rotl64_132 (.in_1(rotl64_109_out_2), .out_2(rotl64_132_out_2));
  rotl64 rotl64_133 (.in_1(rotl64_110_out_2), .out_2(rotl64_133_out_2));
  rotl64 rotl64_134 (.in_1(rotl64_112_out_2), .out_2(rotl64_134_out_2));
  rotl64 rotl64_135 (.in_1(rotl64_113_out_2), .out_2(rotl64_135_out_2));
  rotl64 rotl64_136 (.in_1(rotl64_114_out_2), .out_2(rotl64_136_out_2));
  rotl64 rotl64_137 (.in_1(rotl64_115_out_2), .out_2(rotl64_137_out_2));
  rotl64 rotl64_138 (.in_1(rotl64_116_out_2), .out_2(rotl64_138_out_2));
  rotl64 rotl64_139 (.in_1(rotl64_117_out_2), .out_2(rotl64_139_out_2));
  rotl64 rotl64_140 (.in_1(rotl64_118_out_2), .out_2(rotl64_140_out_2));
  rotl64 rotl64_141 (.in_1(rotl64_119_out_2), .out_2(rotl64_141_out_2));
  rotl64 rotl64_142 (.in_1(rotl64_120_out_2), .out_2(rotl64_142_out_2));
  rotl64 rotl64_143 (.in_1(rotl64_121_out_2), .out_2(rotl64_143_out_2));
  rotl64 rotl64_144 (.in_1(rotl64_122_out_2), .out_2(rotl64_144_out_2));
  rotl64 rotl64_145 (.in_1(rotl64_123_out_2), .out_2(rotl64_145_out_2));
  Adder #(.width(64)) adder_10 (
    .a(adder_8_out), .b(rotl64_124_out_2), .out(adder_10_out), .cin(adder_8_cout), .cout(adder_10_cout));
  Adder #(.width(64)) adder_11 (
    .a(adder_9_out), .b(rotl64_134_out_2), .out(adder_11_out), .cin(adder_9_cout), .cout(adder_11_cout));
  rotl64 rotl64_146 (.in_1(rotl64_125_out_2), .out_2(rotl64_146_out_2));
  rotl64 rotl64_147 (.in_1(rotl64_126_out_2), .out_2(rotl64_147_out_2));
  rotl64 rotl64_148 (.in_1(rotl64_127_out_2), .out_2(rotl64_148_out_2));
  rotl64 rotl64_149 (.in_1(rotl64_128_out_2), .out_2(rotl64_149_out_2));
  rotl64 rotl64_150 (.in_1(rotl64_129_out_2), .out_2(rotl64_150_out_2));
  rotl64 rotl64_151 (.in_1(rotl64_130_out_2), .out_2(rotl64_151_out_2));
  rotl64 rotl64_152 (.in_1(rotl64_131_out_2), .out_2(rotl64_152_out_2));
  rotl64 rotl64_153 (.in_1(rotl64_132_out_2), .out_2(rotl64_153_out_2));
  rotl64 rotl64_154 (.in_1(rotl64_133_out_2), .out_2(rotl64_154_out_2));
  rotl64 rotl64_155 (.in_1(rotl64_135_out_2), .out_2(rotl64_155_out_2));
  rotl64 rotl64_156 (.in_1(rotl64_136_out_2), .out_2(rotl64_156_out_2));
  rotl64 rotl64_157 (.in_1(rotl64_137_out_2), .out_2(rotl64_157_out_2));
  rotl64 rotl64_158 (.in_1(rotl64_138_out_2), .out_2(rotl64_158_out_2));
  rotl64 rotl64_159 (.in_1(rotl64_139_out_2), .out_2(rotl64_159_out_2));
  rotl64 rotl64_160 (.in_1(rotl64_140_out_2), .out_2(rotl64_160_out_2));
  rotl64 rotl64_161 (.in_1(rotl64_141_out_2), .out_2(rotl64_161_out_2));
  rotl64 rotl64_162 (.in_1(rotl64_142_out_2), .out_2(rotl64_162_out_2));
  rotl64 rotl64_163 (.in_1(rotl64_143_out_2), .out_2(rotl64_163_out_2));
  rotl64 rotl64_164 (.in_1(rotl64_144_out_2), .out_2(rotl64_164_out_2));
  rotl64 rotl64_165 (.in_1(rotl64_145_out_2), .out_2(rotl64_165_out_2));
  Adder #(.width(64)) adder_12 (
    .a(adder_10_out), .b(rotl64_146_out_2), .out(adder_12_out), .cin(adder_10_cout), .cout(adder_12_cout));
  Adder #(.width(64)) adder_13 (
    .a(adder_11_out), .b(rotl64_155_out_2), .out(adder_13_out), .cin(adder_11_cout), .cout(adder_13_cout));
  rotl64 rotl64_166 (.in_1(rotl64_147_out_2), .out_2(rotl64_166_out_2));
  rotl64 rotl64_167 (.in_1(rotl64_148_out_2), .out_2(rotl64_167_out_2));
  rotl64 rotl64_168 (.in_1(rotl64_149_out_2), .out_2(rotl64_168_out_2));
  rotl64 rotl64_169 (.in_1(rotl64_150_out_2), .out_2(rotl64_169_out_2));
  rotl64 rotl64_170 (.in_1(rotl64_151_out_2), .out_2(rotl64_170_out_2));
  rotl64 rotl64_171 (.in_1(rotl64_152_out_2), .out_2(rotl64_171_out_2));
  rotl64 rotl64_172 (.in_1(rotl64_153_out_2), .out_2(rotl64_172_out_2));
  rotl64 rotl64_173 (.in_1(rotl64_154_out_2), .out_2(rotl64_173_out_2));
  rotl64 rotl64_174 (.in_1(rotl64_156_out_2), .out_2(rotl64_174_out_2));
  rotl64 rotl64_175 (.in_1(rotl64_157_out_2), .out_2(rotl64_175_out_2));
  rotl64 rotl64_176 (.in_1(rotl64_158_out_2), .out_2(rotl64_176_out_2));
  rotl64 rotl64_177 (.in_1(rotl64_159_out_2), .out_2(rotl64_177_out_2));
  rotl64 rotl64_178 (.in_1(rotl64_160_out_2), .out_2(rotl64_178_out_2));
  rotl64 rotl64_179 (.in_1(rotl64_161_out_2), .out_2(rotl64_179_out_2));
  rotl64 rotl64_180 (.in_1(rotl64_162_out_2), .out_2(rotl64_180_out_2));
  rotl64 rotl64_181 (.in_1(rotl64_163_out_2), .out_2(rotl64_181_out_2));
  rotl64 rotl64_182 (.in_1(rotl64_164_out_2), .out_2(rotl64_182_out_2));
  rotl64 rotl64_183 (.in_1(rotl64_165_out_2), .out_2(rotl64_183_out_2));
  Adder #(.width(64)) adder_14 (
    .a(adder_12_out), .b(rotl64_166_out_2), .out(adder_14_out), .cin(adder_12_cout), .cout(adder_14_cout));
  Adder #(.width(64)) adder_15 (
    .a(adder_13_out), .b(rotl64_174_out_2), .out(adder_15_out), .cin(adder_13_cout), .cout(adder_15_cout));
  rotl64 rotl64_184 (.in_1(rotl64_167_out_2), .out_2(rotl64_184_out_2));
  rotl64 rotl64_185 (.in_1(rotl64_168_out_2), .out_2(rotl64_185_out_2));
  rotl64 rotl64_186 (.in_1(rotl64_169_out_2), .out_2(rotl64_186_out_2));
  rotl64 rotl64_187 (.in_1(rotl64_170_out_2), .out_2(rotl64_187_out_2));
  rotl64 rotl64_188 (.in_1(rotl64_171_out_2), .out_2(rotl64_188_out_2));
  rotl64 rotl64_189 (.in_1(rotl64_172_out_2), .out_2(rotl64_189_out_2));
  rotl64 rotl64_190 (.in_1(rotl64_173_out_2), .out_2(rotl64_190_out_2));
  rotl64 rotl64_191 (.in_1(rotl64_175_out_2), .out_2(rotl64_191_out_2));
  rotl64 rotl64_192 (.in_1(rotl64_176_out_2), .out_2(rotl64_192_out_2));
  rotl64 rotl64_193 (.in_1(rotl64_177_out_2), .out_2(rotl64_193_out_2));
  rotl64 rotl64_194 (.in_1(rotl64_178_out_2), .out_2(rotl64_194_out_2));
  rotl64 rotl64_195 (.in_1(rotl64_179_out_2), .out_2(rotl64_195_out_2));
  rotl64 rotl64_196 (.in_1(rotl64_180_out_2), .out_2(rotl64_196_out_2));
  rotl64 rotl64_197 (.in_1(rotl64_181_out_2), .out_2(rotl64_197_out_2));
  rotl64 rotl64_198 (.in_1(rotl64_182_out_2), .out_2(rotl64_198_out_2));
  rotl64 rotl64_199 (.in_1(rotl64_183_out_2), .out_2(rotl64_199_out_2));
  Adder #(.width(64)) adder_16 (
    .a(adder_14_out), .b(rotl64_184_out_2), .out(adder_16_out), .cin(adder_14_cout), .cout(adder_16_cout));
  Adder #(.width(64)) adder_17 (
    .a(adder_15_out), .b(rotl64_191_out_2), .out(adder_17_out), .cin(adder_15_cout), .cout(adder_17_cout));
  rotl64 rotl64_200 (.in_1(rotl64_185_out_2), .out_2(rotl64_200_out_2));
  rotl64 rotl64_201 (.in_1(rotl64_186_out_2), .out_2(rotl64_201_out_2));
  rotl64 rotl64_202 (.in_1(rotl64_187_out_2), .out_2(rotl64_202_out_2));
  rotl64 rotl64_203 (.in_1(rotl64_188_out_2), .out_2(rotl64_203_out_2));
  rotl64 rotl64_204 (.in_1(rotl64_189_out_2), .out_2(rotl64_204_out_2));
  rotl64 rotl64_205 (.in_1(rotl64_190_out_2), .out_2(rotl64_205_out_2));
  rotl64 rotl64_206 (.in_1(rotl64_192_out_2), .out_2(rotl64_206_out_2));
  rotl64 rotl64_207 (.in_1(rotl64_193_out_2), .out_2(rotl64_207_out_2));
  rotl64 rotl64_208 (.in_1(rotl64_194_out_2), .out_2(rotl64_208_out_2));
  rotl64 rotl64_209 (.in_1(rotl64_195_out_2), .out_2(rotl64_209_out_2));
  rotl64 rotl64_210 (.in_1(rotl64_196_out_2), .out_2(rotl64_210_out_2));
  rotl64 rotl64_211 (.in_1(rotl64_197_out_2), .out_2(rotl64_211_out_2));
  rotl64 rotl64_212 (.in_1(rotl64_198_out_2), .out_2(rotl64_212_out_2));
  rotl64 rotl64_213 (.in_1(rotl64_199_out_2), .out_2(rotl64_213_out_2));
  Adder #(.width(64)) adder_18 (
    .a(adder_16_out), .b(rotl64_200_out_2), .out(adder_18_out), .cin(adder_16_cout), .cout(adder_18_cout));
  Adder #(.width(64)) adder_19 (
    .a(adder_17_out), .b(rotl64_206_out_2), .out(adder_19_out), .cin(adder_17_cout), .cout(adder_19_cout));
  rotl64 rotl64_214 (.in_1(rotl64_201_out_2), .out_2(rotl64_214_out_2));
  rotl64 rotl64_215 (.in_1(rotl64_202_out_2), .out_2(rotl64_215_out_2));
  rotl64 rotl64_216 (.in_1(rotl64_203_out_2), .out_2(rotl64_216_out_2));
  rotl64 rotl64_217 (.in_1(rotl64_204_out_2), .out_2(rotl64_217_out_2));
  rotl64 rotl64_218 (.in_1(rotl64_205_out_2), .out_2(rotl64_218_out_2));
  rotl64 rotl64_219 (.in_1(rotl64_207_out_2), .out_2(rotl64_219_out_2));
  rotl64 rotl64_220 (.in_1(rotl64_208_out_2), .out_2(rotl64_220_out_2));
  rotl64 rotl64_221 (.in_1(rotl64_209_out_2), .out_2(rotl64_221_out_2));
  rotl64 rotl64_222 (.in_1(rotl64_210_out_2), .out_2(rotl64_222_out_2));
  rotl64 rotl64_223 (.in_1(rotl64_211_out_2), .out_2(rotl64_223_out_2));
  rotl64 rotl64_224 (.in_1(rotl64_212_out_2), .out_2(rotl64_224_out_2));
  rotl64 rotl64_225 (.in_1(rotl64_213_out_2), .out_2(rotl64_225_out_2));
  Adder #(.width(64)) adder_20 (
    .a(adder_18_out), .b(rotl64_214_out_2), .out(adder_20_out), .cin(adder_18_cout), .cout(adder_20_cout));
  Adder #(.width(64)) adder_21 (
    .a(adder_19_out), .b(rotl64_219_out_2), .out(adder_21_out), .cin(adder_19_cout), .cout(adder_21_cout));
  rotl64 rotl64_226 (.in_1(rotl64_215_out_2), .out_2(rotl64_226_out_2));
  rotl64 rotl64_227 (.in_1(rotl64_216_out_2), .out_2(rotl64_227_out_2));
  rotl64 rotl64_228 (.in_1(rotl64_217_out_2), .out_2(rotl64_228_out_2));
  rotl64 rotl64_229 (.in_1(rotl64_218_out_2), .out_2(rotl64_229_out_2));
  rotl64 rotl64_230 (.in_1(rotl64_220_out_2), .out_2(rotl64_230_out_2));
  rotl64 rotl64_231 (.in_1(rotl64_221_out_2), .out_2(rotl64_231_out_2));
  rotl64 rotl64_232 (.in_1(rotl64_222_out_2), .out_2(rotl64_232_out_2));
  rotl64 rotl64_233 (.in_1(rotl64_223_out_2), .out_2(rotl64_233_out_2));
  rotl64 rotl64_234 (.in_1(rotl64_224_out_2), .out_2(rotl64_234_out_2));
  rotl64 rotl64_235 (.in_1(rotl64_225_out_2), .out_2(rotl64_235_out_2));
  Adder #(.width(64)) adder_22 (
    .a(adder_20_out), .b(rotl64_226_out_2), .out(adder_22_out), .cin(adder_20_cout), .cout(adder_22_cout));
  Adder #(.width(64)) adder_23 (
    .a(adder_21_out), .b(rotl64_230_out_2), .out(adder_23_out), .cin(adder_21_cout), .cout(adder_23_cout));
  rotl64 rotl64_236 (.in_1(rotl64_227_out_2), .out_2(rotl64_236_out_2));
  rotl64 rotl64_237 (.in_1(rotl64_228_out_2), .out_2(rotl64_237_out_2));
  rotl64 rotl64_238 (.in_1(rotl64_229_out_2), .out_2(rotl64_238_out_2));
  rotl64 rotl64_239 (.in_1(rotl64_231_out_2), .out_2(rotl64_239_out_2));
  rotl64 rotl64_240 (.in_1(rotl64_232_out_2), .out_2(rotl64_240_out_2));
  rotl64 rotl64_241 (.in_1(rotl64_233_out_2), .out_2(rotl64_241_out_2));
  rotl64 rotl64_242 (.in_1(rotl64_234_out_2), .out_2(rotl64_242_out_2));
  rotl64 rotl64_243 (.in_1(rotl64_235_out_2), .out_2(rotl64_243_out_2));
  Adder #(.width(64)) adder_24 (
    .a(adder_22_out), .b(rotl64_236_out_2), .out(adder_24_out), .cin(adder_22_cout), .cout(adder_24_cout));
  Adder #(.width(64)) adder_25 (
    .a(adder_23_out), .b(rotl64_239_out_2), .out(adder_25_out), .cin(adder_23_cout), .cout(adder_25_cout));
  rotl64 rotl64_244 (.in_1(rotl64_237_out_2), .out_2(rotl64_244_out_2));
  rotl64 rotl64_245 (.in_1(rotl64_238_out_2), .out_2(rotl64_245_out_2));
  rotl64 rotl64_246 (.in_1(rotl64_240_out_2), .out_2(rotl64_246_out_2));
  rotl64 rotl64_247 (.in_1(rotl64_241_out_2), .out_2(rotl64_247_out_2));
  rotl64 rotl64_248 (.in_1(rotl64_242_out_2), .out_2(rotl64_248_out_2));
  rotl64 rotl64_249 (.in_1(rotl64_243_out_2), .out_2(rotl64_249_out_2));
  Adder #(.width(64)) adder_26 (
    .a(adder_24_out), .b(rotl64_244_out_2), .out(adder_26_out), .cin(adder_24_cout), .cout(adder_26_cout));
  Adder #(.width(64)) adder_27 (
    .a(adder_25_out), .b(rotl64_246_out_2), .out(adder_27_out), .cin(adder_25_cout), .cout(adder_27_cout));
  rotl64 rotl64_250 (.in_1(rotl64_245_out_2), .out_2(rotl64_250_out_2));
  rotl64 rotl64_251 (.in_1(rotl64_247_out_2), .out_2(rotl64_251_out_2));
  rotl64 rotl64_252 (.in_1(rotl64_248_out_2), .out_2(rotl64_252_out_2));
  rotl64 rotl64_253 (.in_1(rotl64_249_out_2), .out_2(rotl64_253_out_2));
  Adder #(.width(64)) adder_28 (
    .a(adder_26_out), .b(rotl64_250_out_2), .out(adder_28_out), .cin(adder_26_cout), .cout(adder_28_cout));
  Adder #(.width(64)) adder_29 (
    .a(adder_27_out), .b(rotl64_251_out_2), .out(adder_29_out), .cin(adder_27_cout), .cout(adder_29_cout));
  rotl64 rotl64_254 (.in_1(rotl64_252_out_2), .out_2(rotl64_254_out_2));
  rotl64 rotl64_255 (.in_1(rotl64_253_out_2), .out_2(rotl64_255_out_2));
  Adder #(.width(64)) adder_30 (
    .a(adder_29_out), .b(rotl64_254_out_2), .out(adder_30_out), .cin(adder_29_cout), .cout(adder_30_cout));
  rotl64 rotl64_256 (.in_1(rotl64_255_out_2), .out_2(rotl64_256_out_2));
  Adder #(.width(64)) adder_31 (
    .a(adder_30_out), .b(rotl64_256_out_2), .out({Hout, Lout}), .cin(adder_30_cout));  // open: cout
endmodule

module rotl64 (
  input  [63:0] in_1,
  output [63:0] out_2
);


  assign out_2 = {in_1[62:0], in_1[63]};
endmodule

module rotl64p16 (
  input  [63:0] in_1,
  output [63:0] out_2
);

  wire [63:0] rotl64_1_out_2, rotl64_2_out_2, rotl64_3_out_2, rotl64_4_out_2, rotl64_5_out_2, rotl64_6_out_2,
       rotl64_7_out_2, rotl64_8_out_2, rotl64_9_out_2, rotl64_10_out_2, rotl64_11_out_2, rotl64_12_out_2,
       rotl64_13_out_2, rotl64_14_out_2;

  rotl64 rotl64_1 (.in_1(in_1), .out_2(rotl64_1_out_2));
  rotl64 rotl64_2 (.in_1(rotl64_1_out_2), .out_2(rotl64_2_out_2));
  rotl64 rotl64_3 (.in_1(rotl64_2_out_2), .out_2(rotl64_3_out_2));
  rotl64 rotl64_4 (.in_1(rotl64_3_out_2), .out_2(rotl64_4_out_2));
  rotl64 rotl64_5 (.in_1(rotl64_4_out_2), .out_2(rotl64_5_out_2));
  rotl64 rotl64_6 (.in_1(rotl64_5_out_2), .out_2(rotl64_6_out_2));
  rotl64 rotl64_7 (.in_1(rotl64_6_out_2), .out_2(rotl64_7_out_2));
  rotl64 rotl64_8 (.in_1(rotl64_7_out_2), .out_2(rotl64_8_out_2));
  rotl64 rotl64_9 (.in_1(rotl64_8_out_2), .out_2(rotl64_9_out_2));
  rotl64 rotl64_10 (.in_1(rotl64_9_out_2), .out_2(rotl64_10_out_2));
  rotl64 rotl64_11 (.in_1(rotl64_10_out_2), .out_2(rotl64_11_out_2));
  rotl64 rotl64_12 (.in_1(rotl64_11_out_2), .out_2(rotl64_12_out_2));
  rotl64 rotl64_13 (.in_1(rotl64_12_out_2), .out_2(rotl64_13_out_2));
  rotl64 rotl64_14 (.in_1(rotl64_13_out_2), .out_2(rotl64_14_out_2));
  rotl64 rotl64_15 (.in_1(rotl64_14_out_2), .out_2(out_2));
endmodule
